// Logisim project Nawal Ayesha_1911301042 Lab 1.circ as structural Verilog
module IC_7404_NOT (
  input  GND_7,
  input  _1,
  input  _3,
  input  _5,
  input  _9,
  input  _11,
  input  _13,
  input  VCC_14,
  output _2,
  output _4,
  output _6,
  output _8,
  output _10,
  output _12
);

  not not_1 (_2, _1);
  not not_2 (_4, _3);
  not not_3 (_6, _5);
  not not_4 (_8, _9);
  not not_5 (_10, _11);
  not not_6 (_12, _13);
endmodule

module IC_7408_AND (
  input  VCC_14,
  input  _1,
  input  _2,
  input  _4,
  input  _5,
  input  _9,
  input  _10,
  input  _12,
  input  _13,
  input  GND_7,
  output _3,
  output _6,
  output _8,
  output _11
);

  and and_1 (_3, _1, _2);
  and and_2 (_6, _4, _5);
  and and_3 (_8, _9, _10);
  and and_4 (_11, _12, _13);
endmodule

module IC_7432_OR (
  input  VCC_14,
  input  _1,
  input  _2,
  input  _4,
  input  _5,
  input  _9,
  input  _10,
  input  _12,
  input  _13,
  input  GND_7,
  output _3,
  output _6,
  output _8,
  output _11
);

  or or_1 (_3, _1, _2);
  or or_2 (_6, _4, _5);
  or or_3 (_8, _9, _10);
  or or_4 (_11, _12, _13);
endmodule

module IC_7486_XOR (
  input  VCC_14,
  input  _1,
  input  _2,
  input  _4,
  input  _5,
  input  _9,
  input  _10,
  input  _12,
  input  _13,
  input  GND_7,
  output _3,
  output _6,
  output _8,
  output _11
);

  xor xor_1 (_3, _1, _2);
  xor xor_2 (_6, _4, _5);
  xor xor_3 (_8, _9, _10);
  xor xor_4 (_11, _12, _13);
endmodule

module _4_1_MUX (
  input  I3,
  input  I2,
  input  I1,
  input  I0,
  input  S1,
  input  S0,
  output F
);

  wire and_1_out, and_2_out, and_3_out, and_4_out, not_1_out, not_2_out, or_1_out, or_2_out;

  not not_1 (not_1_out, S1);
  not not_2 (not_2_out, S0);
  and and_1 (and_1_out, not_1_out, not_2_out, I0);
  and and_2 (and_2_out, S0, not_1_out, I1);
  and and_3 (and_3_out, not_2_out, S1, I2);
  and and_4 (and_4_out, S0, S1, I3);
  or or_1 (or_1_out, and_1_out, and_2_out);
  or or_2 (or_2_out, and_3_out, and_4_out);
  or or_3 (F, or_1_out, or_2_out);
endmodule

module _2_Bit_ALU (
  input  [1:0] A1_A0,
  input  [1:0] B1_B0,
  input  [1:0] S1_S0,
  output [1:0] F1_F0
);

  wire ic_7404_not_1__2, ic_7404_not_1__12, ic_7408_and_1__3, ic_7408_and_1__6, ic_7432_or_1__3,
       ic_7432_or_1__6, ic_7486_xor_1__3, ic_7486_xor_1__6;

  IC_7408_AND ic_7408_and_1 (
    ._1(A1_A0[1]), ._2(B1_B0[1]), ._4(B1_B0[0]), ._5(A1_A0[0]), ._3(ic_7408_and_1__3), ._6(ic_7408_and_1__6));  // open: VCC_14, _9, _10, _12, _13, GND_7, _8, _11
  IC_7432_OR ic_7432_or_1 (
    ._1(A1_A0[1]), ._2(B1_B0[1]), ._4(B1_B0[0]), ._5(A1_A0[0]), ._3(ic_7432_or_1__3), ._6(ic_7432_or_1__6));  // open: VCC_14, _9, _10, _12, _13, GND_7, _8, _11
  IC_7486_XOR ic_7486_xor_1 (
    ._1(B1_B0[1]), ._2(A1_A0[1]), ._4(B1_B0[0]), ._5(A1_A0[0]), ._3(ic_7486_xor_1__3), ._6(ic_7486_xor_1__6));  // open: VCC_14, _9, _10, _12, _13, GND_7, _8, _11
  IC_7404_NOT ic_7404_not_1 (
    ._1(A1_A0[1]), ._13(A1_A0[0]), ._2(ic_7404_not_1__2), ._12(ic_7404_not_1__12));  // open: GND_7, _3, _5, _9, _11, VCC_14, _4, _6, _8, _10
  Multiplexer #(.select(2), .enable("false")) multiplexer_1 (
    .in0(ic_7408_and_1__3), .in1(ic_7432_or_1__3), .in2(ic_7486_xor_1__3), .in3(ic_7404_not_1__2),
    .out(F1_F0[1]), .sel(S1_S0));
  Multiplexer #(.select(2), .enable("false")) multiplexer_2 (
    .in0(ic_7408_and_1__6), .in1(ic_7432_or_1__6), .in2(ic_7486_xor_1__6), .in3(ic_7404_not_1__12),
    .out(F1_F0[0]), .sel(S1_S0));

  // Notes on the sheet:
  //   Nawal Ayesha Khan, 1911301042
  //   A0+B0
  //   A0^B0
  //   A1B1
  //   A1+B1
  //   A1^B1
  //   A1'
  //   A0B0
  //   A0'
endmodule
