// Logisim project Nawal Ayesha_1911301042 Lab 2.circ as structural Verilog: 3 circuits, main circuit main
module main (
  input  [3:0] in_1,
  input  [3:0] in_2,
  output [7:0] out_3
);

  _4_bit_multiplier u_4_bit_multiplier_1 (.A(in_1), .A_2(in_2), .S(out_3));
endmodule

module IC_7483 (
  input  in_1,
  input  A3,
  input  A2,
  input  A1,
  input  A0,
  input  B3,
  input  B2,
  input  B1,
  input  B0,
  output C_out,
  output S3,
  output S2,
  output S1,
  output S0
);

  wire and_1_out, and_2_out, and_3_out, and_4_out, and_5_out, and_6_out, and_7_out, and_8_out, or_1_out,
       or_2_out, or_3_out, xor_1_out, xor_2_out, xor_3_out, xor_4_out;

  xor xor_1 (xor_1_out, A0, B0);
  and and_1 (and_1_out, A0, B0);
  xor xor_2 (xor_2_out, A1, B1);
  and and_2 (and_2_out, A1, B1);
  xor xor_3 (xor_3_out, A2, B2);
  and and_3 (and_3_out, A2, B2);
  xor xor_4 (xor_4_out, A3, B2);
  and and_4 (and_4_out, A3, B2);
  xor xor_5 (S0, xor_1_out, in_1);
  and and_5 (and_5_out, xor_1_out, in_1);
  xor xor_6 (S1, xor_2_out, or_1_out);
  and and_6 (and_6_out, xor_2_out, or_1_out);
  xor xor_7 (S2, xor_3_out, or_2_out);
  and and_7 (and_7_out, xor_3_out, or_2_out);
  xor xor_8 (S3, xor_4_out, or_3_out);
  and and_8 (and_8_out, xor_4_out, or_3_out);
  or or_1 (or_1_out, and_5_out, and_1_out);
  or or_2 (or_2_out, and_6_out, and_2_out);
  or or_3 (or_3_out, and_7_out, and_3_out);
  or or_4 (C_out, and_8_out, and_4_out);
endmodule

module _4_bit_multiplier (
  input  [3:0] A,
  input  [3:0] A_2,
  output [7:0] S
);

  wire [2:0] and_1_out;
  wire [3:0] adder_2_out, and_4_out, and_9_out, and_13_out;
  wire [3:1] adder_1_out;
  wire [3:3] adder_1_cout;

  and and_1 (and_1_out[0], A[0], A_2[1]);
  and and_2 (and_1_out[1], A[0], A_2[2]);
  and and_3 (and_1_out[2], A[0], A_2[3]);
  and and_4 (and_4_out[0], A[1], A_2[0]);
  and and_5 (and_4_out[1], A[1], A_2[1]);
  and and_6 (and_4_out[2], A[1], A_2[2]);
  and and_7 (and_4_out[3], A[1], A_2[3]);
  and and_8 (S[0], A[0], A_2[0]);
  Adder #(.width(4)) adder_1 (
    .a({1'b0, and_1_out}), .b(and_4_out), .out({adder_1_out, S[1]}), .cin(1'b0), .cout(adder_1_cout[3]));
  and and_9 (and_9_out[0], A[2], A_2[0]);
  and and_10 (and_9_out[1], A[2], A_2[1]);
  and and_11 (and_9_out[2], A[2], A_2[2]);
  and and_12 (and_9_out[3], A[2], A_2[3]);
  Adder #(.width(4)) adder_2 (
    .a({adder_1_cout[3], adder_1_out}), .b(and_9_out), .out({adder_2_out[2:0], S[2]}), .cin(1'b0),
    .cout(adder_2_out[3]));
  and and_13 (and_13_out[0], A[3], A_2[0]);
  and and_14 (and_13_out[1], A[3], A_2[1]);
  and and_15 (and_13_out[2], A[3], A_2[2]);
  and and_16 (and_13_out[3], A[3], A_2[3]);
  Adder #(.width(4)) adder_3 (.a(adder_2_out), .b(and_13_out), .out(S[6:3]), .cin(1'b0), .cout(S[7]));

  // Notes on the sheet:
  //   A1B2
  //   A1B3
  //   A1B4
  //   A2B1
  //   A2B2
  //   A2B3
  //   A2B4
  //   A1B1
  //   Nawal Ayesha Khan, 1911301042
  //   A3B1
  //   A3B2
  //   A3B3
  //   A3B4
  //   A4B1
  //   A4B2
  //   A4B3
  //   A4B4
endmodule
