// Logisim project Nawal Ayesha_1911301042 Lab 3.circ as structural Verilog
module IC_7404_NOT (
  input  GND_7,
  input  _1,
  input  _3,
  input  _5,
  input  _9,
  input  _11,
  input  _13,
  input  VCC_14,
  output _2,
  output _4,
  output _6,
  output _8,
  output _10,
  output _12
);

  not not_1 (_2, _1);
  not not_2 (_4, _3);
  not not_3 (_6, _5);
  not not_4 (_8, _9);
  not not_5 (_10, _11);
  not not_6 (_12, _13);
endmodule

module IC_7408_AND (
  input  VCC_14,
  input  _1,
  input  _2,
  input  _4,
  input  _5,
  input  _9,
  input  _10,
  input  _12,
  input  _13,
  input  GND_7,
  output _3,
  output _6,
  output _8,
  output _11
);

  and and_1 (_3, _1, _2);
  and and_2 (_6, _4, _5);
  and and_3 (_8, _9, _10);
  and and_4 (_11, _12, _13);
endmodule

module IC_7432_OR (
  input  VCC_14,
  input  _1,
  input  _2,
  input  _4,
  input  _5,
  input  _9,
  input  _10,
  input  _12,
  input  _13,
  input  GND_7,
  output _3,
  output _6,
  output _8,
  output _11
);

  or or_1 (_3, _1, _2);
  or or_2 (_6, _4, _5);
  or or_3 (_8, _9, _10);
  or or_4 (_11, _12, _13);
endmodule

module _2_bit_Arithmetic_Unit (
  input  Cin,
  input  [1:0] S1S0,
  input  [1:0] A1A0,
  input  [1:0] B1B0,
  output [1:0] D1D0,
  output Cout
);

  wire adder_1_cout, multiplexer_1_out, multiplexer_2_out, not_1_out, not_2_out;

  not not_1 (not_1_out, B1B0[1]);
  not not_2 (not_2_out, B1B0[0]);
  Multiplexer #(.select(2), .enable("false")) multiplexer_1 (
    .in0(B1B0[0]), .in1(not_2_out), .in2(1'b0), .in3(1'b1), .out(multiplexer_1_out), .sel(S1S0));
  Multiplexer #(.select(2), .enable("false")) multiplexer_2 (
    .in0(B1B0[1]), .in1(not_1_out), .in2(1'b0), .in3(1'b1), .out(multiplexer_2_out), .sel(S1S0));
  Adder #(.width(1)) adder_1 (.a(A1A0[0]), .b(multiplexer_1_out), .out(D1D0[0]), .cin(Cin), .cout(adder_1_cout));
  Adder #(.width(1)) adder_2 (.a(A1A0[1]), .b(multiplexer_2_out), .out(D1D0[1]), .cin(adder_1_cout), .cout(Cout));

  // Notes on the sheet:
  //   Nawal Ayesha Khan 1911301042
  //   A0
  //   A1
  //   D0
  //   D1
endmodule
