// Logisim project Nawal Ayesha_1911301042 Lab 4.circ as structural Verilog: 2 circuits, main circuit main
module main (
  input  [3:0] in_1,
  input  [3:0] in_2,
  input  [3:0] in_3,
  input  [15:0] in_4,
  input  in_5,
  output [15:0] out_6,
  output [15:0] out_7
);

  wire clock_1_out;

  Clock clock_1 (.out(clock_1_out));
  Register_file register_file_1 (
    .Write_Register_rd(in_3), .Write_Data(in_4), .RegWrite(in_5), .CLK(clock_1_out), .Read_data_1(out_6),
    .Read_data_2(out_7), .Read_Register_1_rs(in_1), .Read_Register_2__rt(in_2));
endmodule

module Register_file (
  input  [3:0] Read_Register_1_rs,
  input  [3:0] Write_Register_rd,
  input  [15:0] Write_Data,
  input  [3:0] Read_Register_2__rt,
  input  RegWrite,
  input  CLK,
  output [15:0] Read_data_1,
  output [15:0] Read_data_2
);

  wire and_1_out, and_2_out, and_3_out, and_4_out, and_5_out, and_6_out, and_7_out, and_8_out, and_9_out,
       and_10_out, and_11_out, and_12_out, and_13_out, and_14_out, and_15_out, decoder_1_out0,
       decoder_1_out1, decoder_1_out2, decoder_1_out3, decoder_1_out4, decoder_1_out5, decoder_1_out6,
       decoder_1_out7, decoder_1_out8, decoder_1_out9, decoder_1_out10, decoder_1_out11, decoder_1_out12,
       decoder_1_out13, decoder_1_out14, decoder_1_out15;
  wire [15:0] _11_q, _12_q, _13_q, _14_q, register_1_q, register_2_q, register_3_q, register_4_q,
       register_5_q, register_6_q, register_7_q, register_8_q, register_9_q, register_10_q, register_11_q,
       register_12_q;

  Decoder #(.select(4), .enable("false")) decoder_1 (
    .out0(decoder_1_out0), .out1(decoder_1_out1), .out2(decoder_1_out2), .out3(decoder_1_out3),
    .out4(decoder_1_out4), .out5(decoder_1_out5), .out6(decoder_1_out6), .out7(decoder_1_out7),
    .out8(decoder_1_out8), .out9(decoder_1_out9), .out10(decoder_1_out10), .out11(decoder_1_out11),
    .out12(decoder_1_out12), .out13(decoder_1_out13), .out14(decoder_1_out14), .out15(decoder_1_out15),
    .sel(Write_Register_rd));
  and and_1 (and_1_out, decoder_1_out0, RegWrite);
  and and_2 (and_2_out, decoder_1_out1, RegWrite);
  and and_3 (and_3_out, decoder_1_out14, RegWrite);
  and and_4 (and_4_out, decoder_1_out15, RegWrite);
  and and_5 (and_5_out, decoder_1_out2, RegWrite);
  and and_6 (and_6_out, decoder_1_out3, RegWrite);
  and and_7 (and_7_out, decoder_1_out4, RegWrite);
  and and_8 (and_8_out, RegWrite, decoder_1_out5);
  and and_9 (and_9_out, decoder_1_out6, RegWrite);
  and and_10 (and_10_out, decoder_1_out7, RegWrite);
  and and_11 (and_11_out, decoder_1_out8, RegWrite);
  and and_12 (and_12_out, decoder_1_out9, RegWrite);
  and and_13 (and_13_out, decoder_1_out10, RegWrite);
  and and_14 (and_14_out, decoder_1_out11, RegWrite);
  and and_15 (and_15_out, decoder_1_out12, RegWrite);
  Register #(.width(16)) register_1 (.D(Write_Data), .en(and_1_out), .Q(register_1_q), .clk(CLK));  // open: clr
  Register #(.width(16)) register_2 (.D(Write_Data), .en(and_2_out), .Q(register_2_q), .clk(CLK));  // open: clr
  Register #(.width(16)) register_3 (.D(Write_Data), .en(and_5_out), .Q(register_3_q), .clk(CLK));  // open: clr
  Register #(.width(16)) register_4 (.D(Write_Data), .en(and_6_out), .Q(register_4_q), .clk(CLK));  // open: clr
  Register #(.width(16)) register_5 (.D(Write_Data), .en(and_7_out), .Q(register_5_q), .clk(CLK));  // open: clr
  Register #(.width(16)) register_6 (.D(Write_Data), .en(and_8_out), .Q(register_6_q), .clk(CLK));  // open: clr
  Register #(.width(16)) register_7 (.D(Write_Data), .en(and_9_out), .Q(register_7_q), .clk(CLK));  // open: clr
  Register #(.width(16)) register_8 (.D(Write_Data), .en(and_10_out), .Q(register_8_q), .clk(CLK));  // open: clr
  Register #(.width(16)) register_9 (.D(Write_Data), .en(and_11_out), .Q(register_9_q), .clk(CLK));  // open: clr
  Register #(.width(16)) register_10 (.D(Write_Data), .en(and_12_out), .Q(register_10_q), .clk(CLK));  // open: clr
  Register #(.width(16)) register_11 (.D(Write_Data), .en(and_13_out), .Q(register_11_q), .clk(CLK));  // open: clr
  Register #(.width(16)) _11 (.D(Write_Data), .en(and_14_out), .Q(_11_q), .clk(CLK));  // open: clr
  Register #(.width(16)) register_12 (.D(Write_Data), .en(and_4_out), .Q(register_12_q), .clk(CLK));  // open: clr
  Register #(.width(16)) _12 (.D(Write_Data), .en(and_15_out), .Q(_12_q), .clk(CLK));  // open: clr
  Register #(.width(16)) _13 (.D(Write_Data), .en(decoder_1_out13), .Q(_13_q), .clk(CLK));  // open: clr
  Register #(.width(16)) _14 (.D(Write_Data), .en(and_3_out), .Q(_14_q));  // open: clk, clr
  Multiplexer #(.select(4), .width(16), .enable("false")) multiplexer_1 (
    .in0(register_1_q), .in1(register_2_q), .in2(register_3_q), .in3(register_4_q), .in4(register_5_q),
    .in5(register_6_q), .in6(register_7_q), .in7(register_8_q), .in8(register_9_q), .in9(register_10_q),
    .in10(register_11_q), .in11(_11_q), .in12(_12_q), .in13(_13_q), .in14(_14_q), .in15(register_12_q),
    .out(Read_data_1), .sel(Read_Register_1_rs));
  Multiplexer #(.select(4), .width(16), .enable("false")) multiplexer_2 (
    .in0(register_1_q), .in1(register_2_q), .in2(register_3_q), .in3(register_4_q), .in4(register_5_q),
    .in5(register_6_q), .in6(register_7_q), .in7(register_8_q), .in8(register_9_q), .in9(register_10_q),
    .in10(register_11_q), .in11(_11_q), .in12(_12_q), .in13(_13_q), .in14(_14_q), .in15(register_12_q),
    .out(Read_data_2), .sel(Read_Register_2__rt));

  // Notes on the sheet:
  //   Nawal Ayesha Khan 1911301042
  //   0
  //   1
  //   2
  //   3
  //   4
  //   5
  //   6
  //   7
  //   8
  //   9
  //   10
  //   15
endmodule
