// Logisim project Nawal Ayesha_1911301042 Lab 5.circ as structural Verilog: 3 circuits, main circuit main
module main (
  input  [2:0] in_1,
  input  in_2,
  input  in_3,
  input  [15:0] in_4,
  input  [15:0] in_5,
  output [15:0] out_6,
  output out_7
);

  _16_bit_ALU u_16_bit_alu_1 (
    .C_In(in_3), .B_inv(in_2), .ALU_Op(in_1), .A(in_4), .B(in_5), .Result(out_6), .Carry_Out(out_7));

  // Notes on the sheet:
  //   001-OR
  //   000-AND
  //   010-ADD
  //   011-SUB
endmodule

module _1_bit_ALU (
  input  A,
  input  B,
  input  C_in,
  input  [2:0] ALUOp,
  input  B_In,
  output Result,
  output Carry_Out
);

  wire adder_1_out, and_1_out, multiplexer_1_out, not_1_out, or_1_out;

  not not_1 (not_1_out, B);
  Multiplexer #(.enable("false")) multiplexer_1 (.in0(B), .in1(not_1_out), .out(multiplexer_1_out), .sel(B_In));
  and and_1 (and_1_out, A, B);
  or or_1 (or_1_out, A, B);
  Adder #(.width(1)) adder_1 (.a(A), .b(multiplexer_1_out), .out(adder_1_out), .cin(C_in), .cout(Carry_Out));
  Multiplexer #(.select(3), .enable("false")) multiplexer_2 (
    .in0(and_1_out), .in1(or_1_out), .in2(adder_1_out), .in3(adder_1_out), .out(Result), .sel(ALUOp));  // open: in4, in5, in6, in7

  // Notes on the sheet:
  //   001-OR
  //   000-AND
  //   010-ADD
  //   011-SUB
  //   OR
  //   ADD
  //   Nawal Ayesha Khan 1911301042
  //   AND
  //   SUB
endmodule

module _16_bit_ALU (
  input  B_inv,
  input  [2:0] ALU_Op,
  input  C_In,
  input  [15:0] A,
  input  [15:0] B,
  output [15:0] Result,
  output Carry_Out
);

  wire n1_bit_alu_1_carry_out, n1_bit_alu_2_carry_out, n1_bit_alu_3_carry_out, n1_bit_alu_4_carry_out,
       n1_bit_alu_5_carry_out, n1_bit_alu_6_carry_out, n1_bit_alu_7_carry_out, n1_bit_alu_8_carry_out,
       n1_bit_alu_9_carry_out, n1_bit_alu_10_carry_out, n1_bit_alu_11_carry_out, n1_bit_alu_12_carry_out,
       n1_bit_alu_13_carry_out, n1_bit_alu_14_carry_out, n1_bit_alu_15_carry_out;

  _1_bit_ALU u_1_bit_alu_1 (
    .A(A[0]), .B(B[0]), .C_in(C_In), .ALUOp(ALU_Op), .B_In(B_inv), .Result(Result[0]),
    .Carry_Out(n1_bit_alu_1_carry_out));
  _1_bit_ALU u_1_bit_alu_2 (
    .A(A[1]), .B(B[1]), .C_in(n1_bit_alu_1_carry_out), .ALUOp(ALU_Op), .B_In(B_inv), .Result(Result[1]),
    .Carry_Out(n1_bit_alu_2_carry_out));
  _1_bit_ALU u_1_bit_alu_3 (
    .A(A[2]), .B(B[2]), .C_in(n1_bit_alu_2_carry_out), .ALUOp(ALU_Op), .B_In(B_inv), .Result(Result[2]),
    .Carry_Out(n1_bit_alu_3_carry_out));
  _1_bit_ALU u_1_bit_alu_4 (
    .A(A[3]), .B(B[3]), .C_in(n1_bit_alu_3_carry_out), .ALUOp(ALU_Op), .B_In(B_inv), .Result(Result[3]),
    .Carry_Out(n1_bit_alu_4_carry_out));
  _1_bit_ALU u_1_bit_alu_5 (
    .A(A[4]), .B(B[4]), .C_in(n1_bit_alu_4_carry_out), .ALUOp(ALU_Op), .B_In(B_inv), .Result(Result[4]),
    .Carry_Out(n1_bit_alu_5_carry_out));
  _1_bit_ALU u_1_bit_alu_6 (
    .A(A[5]), .B(B[5]), .C_in(n1_bit_alu_5_carry_out), .ALUOp(ALU_Op), .B_In(B_inv), .Result(Result[5]),
    .Carry_Out(n1_bit_alu_6_carry_out));
  _1_bit_ALU u_1_bit_alu_7 (
    .A(A[6]), .B(B[6]), .C_in(n1_bit_alu_6_carry_out), .ALUOp(ALU_Op), .B_In(B_inv), .Result(Result[6]),
    .Carry_Out(n1_bit_alu_7_carry_out));
  _1_bit_ALU u_1_bit_alu_8 (
    .A(A[7]), .B(B[7]), .C_in(n1_bit_alu_7_carry_out), .ALUOp(ALU_Op), .B_In(B_inv), .Result(Result[7]),
    .Carry_Out(n1_bit_alu_8_carry_out));
  _1_bit_ALU u_1_bit_alu_9 (
    .A(A[8]), .B(B[8]), .C_in(n1_bit_alu_8_carry_out), .ALUOp(ALU_Op), .B_In(B_inv), .Result(Result[8]),
    .Carry_Out(n1_bit_alu_9_carry_out));
  _1_bit_ALU u_1_bit_alu_10 (
    .A(A[9]), .B(B[9]), .C_in(n1_bit_alu_9_carry_out), .ALUOp(ALU_Op), .B_In(B_inv), .Result(Result[9]),
    .Carry_Out(n1_bit_alu_10_carry_out));
  _1_bit_ALU u_1_bit_alu_11 (
    .A(A[10]), .B(B[10]), .C_in(n1_bit_alu_10_carry_out), .ALUOp(ALU_Op), .B_In(B_inv), .Result(Result[10]),
    .Carry_Out(n1_bit_alu_11_carry_out));
  _1_bit_ALU u_1_bit_alu_12 (
    .A(A[11]), .B(B[11]), .C_in(n1_bit_alu_11_carry_out), .ALUOp(ALU_Op), .B_In(B_inv), .Result(Result[11]),
    .Carry_Out(n1_bit_alu_12_carry_out));
  _1_bit_ALU u_1_bit_alu_13 (
    .A(A[12]), .B(B[12]), .C_in(n1_bit_alu_12_carry_out), .ALUOp(ALU_Op), .B_In(B_inv), .Result(Result[12]),
    .Carry_Out(n1_bit_alu_13_carry_out));
  _1_bit_ALU u_1_bit_alu_14 (
    .A(A[13]), .B(B[13]), .C_in(n1_bit_alu_13_carry_out), .ALUOp(ALU_Op), .B_In(B_inv), .Result(Result[13]),
    .Carry_Out(n1_bit_alu_14_carry_out));
  _1_bit_ALU u_1_bit_alu_15 (
    .A(A[14]), .B(B[14]), .C_in(n1_bit_alu_14_carry_out), .ALUOp(ALU_Op), .B_In(B_inv), .Result(Result[14]),
    .Carry_Out(n1_bit_alu_15_carry_out));
  _1_bit_ALU u_1_bit_alu_16 (
    .A(A[15]), .B(B[15]), .C_in(n1_bit_alu_15_carry_out), .ALUOp(ALU_Op), .B_In(B_inv), .Result(Result[15]),
    .Carry_Out(Carry_Out));

  // Notes on the sheet:
  //   Nawal Ayesha Khan 1911301042
endmodule
