// Logisim project Nawal Ayesha_1911301042 Lab 7.circ as structural Verilog: 7 circuits, main circuit main
module main (
  input  [15:0] in_1,
  input  CLR,
  input  CLK,
  input  RegWrite,
  output [15:0] Next_Address,
  output [15:0] out_6,
  output [3:0] Opcode,
  output [15:0] Reg_1_data,
  output [15:0] out_9,
  output [15:0] out_10,
  output [15:0] Reg_data_2,
  output [15:0] offset
);

  Instruction_Fetch instruction_fetch_1 (.CLK(CLK), .CLR(CLR), .Instruction(out_10), .Next_Address(Next_Address));
  IF_ID_Pipeline_register if_id_pipeline_register_1 (
    .Next_Address(Next_Address), .CLK(CLK), .CLR(CLR), .Instruction(out_10), .out_5(out_6),
    .Instruction_2({Opcode, out_9[11:0]}));
  assign offset = {{12{1'b0}}, out_9[3:0]};  // Bit_Extender bit_extender_1
  Register register_1 (
    .Write_Register_rd(out_9[3:0]), .Write_Data(in_1), .RegWrite(RegWrite), .CLK(CLK),
    .Read_data_1(Reg_1_data), .Read_data_2(Reg_data_2), .Read_Register_1_rs(out_9[11:8]),
    .Read_Register_2__rt(out_9[7:4]));

  assign out_9[15:12] = Opcode;

  // Notes on the sheet:
  //   Nawal Ayesha Khan, 1911301042
  //   rs
  //   rt
  //   rd
endmodule

module Register (
  input  [3:0] Read_Register_1_rs,
  input  [3:0] Write_Register_rd,
  input  [15:0] Write_Data,
  input  [3:0] Read_Register_2__rt,
  input  RegWrite,
  input  CLK,
  output [15:0] Read_data_1,
  output [15:0] Read_data_2
);

  wire and_1_out, and_2_out, and_3_out, and_4_out, and_5_out, and_6_out, and_7_out, and_8_out, and_9_out,
       and_10_out, and_11_out, and_12_out, and_13_out, and_14_out, and_15_out, decoder_1_out0,
       decoder_1_out1, decoder_1_out2, decoder_1_out3, decoder_1_out4, decoder_1_out5, decoder_1_out6,
       decoder_1_out7, decoder_1_out8, decoder_1_out9, decoder_1_out10, decoder_1_out11, decoder_1_out12,
       decoder_1_out13, decoder_1_out14, decoder_1_out15;
  wire [15:0] _11_q, _12_q, _13_q, _14_q, register_1_q, register_2_q, register_3_q, register_4_q,
       register_5_q, register_6_q, register_7_q, register_8_q, register_9_q, register_10_q, register_11_q,
       register_12_q;

  Decoder #(.select(4), .enable("false")) decoder_1 (
    .out0(decoder_1_out0), .out1(decoder_1_out1), .out2(decoder_1_out2), .out3(decoder_1_out3),
    .out4(decoder_1_out4), .out5(decoder_1_out5), .out6(decoder_1_out6), .out7(decoder_1_out7),
    .out8(decoder_1_out8), .out9(decoder_1_out9), .out10(decoder_1_out10), .out11(decoder_1_out11),
    .out12(decoder_1_out12), .out13(decoder_1_out13), .out14(decoder_1_out14), .out15(decoder_1_out15),
    .sel(Write_Register_rd));
  and and_1 (and_1_out, decoder_1_out0, RegWrite);
  and and_2 (and_2_out, decoder_1_out1, RegWrite);
  and and_3 (and_3_out, decoder_1_out14, RegWrite);
  and and_4 (and_4_out, decoder_1_out15, RegWrite);
  and and_5 (and_5_out, decoder_1_out2, RegWrite);
  and and_6 (and_6_out, decoder_1_out3, RegWrite);
  and and_7 (and_7_out, decoder_1_out4, RegWrite);
  and and_8 (and_8_out, RegWrite, decoder_1_out5);
  and and_9 (and_9_out, decoder_1_out6, RegWrite);
  and and_10 (and_10_out, decoder_1_out7, RegWrite);
  and and_11 (and_11_out, decoder_1_out8, RegWrite);
  and and_12 (and_12_out, decoder_1_out9, RegWrite);
  and and_13 (and_13_out, decoder_1_out10, RegWrite);
  and and_14 (and_14_out, decoder_1_out11, RegWrite);
  and and_15 (and_15_out, decoder_1_out12, RegWrite);
  Register_part #(.width(16)) register_1 (.D(Write_Data), .en(and_1_out), .Q(register_1_q), .clk(CLK));  // open: clr
  Register_part #(.width(16)) register_2 (.D(Write_Data), .en(and_2_out), .Q(register_2_q), .clk(CLK));  // open: clr
  Register_part #(.width(16)) register_3 (.D(Write_Data), .en(and_5_out), .Q(register_3_q), .clk(CLK));  // open: clr
  Register_part #(.width(16)) register_4 (.D(Write_Data), .en(and_6_out), .Q(register_4_q), .clk(CLK));  // open: clr
  Register_part #(.width(16)) register_5 (.D(Write_Data), .en(and_7_out), .Q(register_5_q), .clk(CLK));  // open: clr
  Register_part #(.width(16)) register_6 (.D(Write_Data), .en(and_8_out), .Q(register_6_q), .clk(CLK));  // open: clr
  Register_part #(.width(16)) register_7 (.D(Write_Data), .en(and_9_out), .Q(register_7_q), .clk(CLK));  // open: clr
  Register_part #(.width(16)) register_8 (.D(Write_Data), .en(and_10_out), .Q(register_8_q), .clk(CLK));  // open: clr
  Register_part #(.width(16)) register_9 (.D(Write_Data), .en(and_11_out), .Q(register_9_q), .clk(CLK));  // open: clr
  Register_part #(.width(16)) register_10 (.D(Write_Data), .en(and_12_out), .Q(register_10_q), .clk(CLK));  // open: clr
  Register_part #(.width(16)) register_11 (.D(Write_Data), .en(and_13_out), .Q(register_11_q), .clk(CLK));  // open: clr
  Register_part #(.width(16)) _11 (.D(Write_Data), .en(and_14_out), .Q(_11_q), .clk(CLK));  // open: clr
  Register_part #(.width(16)) register_12 (.D(Write_Data), .en(and_4_out), .Q(register_12_q), .clk(CLK));  // open: clr
  Register_part #(.width(16)) _12 (.D(Write_Data), .en(and_15_out), .Q(_12_q), .clk(CLK));  // open: clr
  Register_part #(.width(16)) _13 (.D(Write_Data), .en(decoder_1_out13), .Q(_13_q), .clk(CLK));  // open: clr
  Register_part #(.width(16)) _14 (.D(Write_Data), .en(and_3_out), .Q(_14_q));  // open: clk, clr
  Multiplexer #(.select(4), .width(16), .enable("false")) multiplexer_1 (
    .in0(register_1_q), .in1(register_2_q), .in2(register_3_q), .in3(register_4_q), .in4(register_5_q),
    .in5(register_6_q), .in6(register_7_q), .in7(register_8_q), .in8(register_9_q), .in9(register_10_q),
    .in10(register_11_q), .in11(_11_q), .in12(_12_q), .in13(_13_q), .in14(_14_q), .in15(register_12_q),
    .out(Read_data_1), .sel(Read_Register_1_rs));
  Multiplexer #(.select(4), .width(16), .enable("false")) multiplexer_2 (
    .in0(register_1_q), .in1(register_2_q), .in2(register_3_q), .in3(register_4_q), .in4(register_5_q),
    .in5(register_6_q), .in6(register_7_q), .in7(register_8_q), .in8(register_9_q), .in9(register_10_q),
    .in10(register_11_q), .in11(_11_q), .in12(_12_q), .in13(_13_q), .in14(_14_q), .in15(register_12_q),
    .out(Read_data_2), .sel(Read_Register_2__rt));

  // Notes on the sheet:
  //   Nawal Ayesha Khan 1911301042
  //   0
  //   1
  //   2
  //   3
  //   4
  //   5
  //   6
  //   7
  //   8
  //   9
  //   10
  //   15
endmodule

module Instruction_Fetch (
  input  CLK,
  input  CLR,
  output [15:0] Next_Address,
  output [15:0] Instruction
);

  wire [15:0] register_1_q;

  Register_part #(.width(16)) register_1 (.D(Next_Address), .Q(register_1_q), .clk(CLK), .clr(CLR));  // open: en
  Adder #(.width(16)) adder_1 (.a(16'h1), .b(register_1_q), .out(Next_Address), .cin(1'b0));  // open: cout
  ROM #(.addrWidth(16), .dataWidth(16)) rom_1 (.addr(register_1_q), .data(Instruction));  // open: sel

  // Notes on the sheet:
  //   contents of rom_1 (hex, n*v repeats v):
  //   2a23 2c47 107f 1588
endmodule

module _1_bit_ALU (
  input  A,
  input  B,
  input  C_in,
  input  [2:0] ALUOp,
  input  B_In,
  output Result,
  output Carry_Out
);

  wire adder_1_out, and_1_out, multiplexer_1_out, not_1_out, or_1_out;

  not not_1 (not_1_out, B);
  Multiplexer #(.enable("false")) multiplexer_1 (.in0(B), .in1(not_1_out), .out(multiplexer_1_out), .sel(B_In));
  and and_1 (and_1_out, A, B);
  or or_1 (or_1_out, A, B);
  Adder #(.width(1)) adder_1 (.a(A), .b(multiplexer_1_out), .out(adder_1_out), .cin(C_in), .cout(Carry_Out));
  Multiplexer #(.select(3), .enable("false")) multiplexer_2 (
    .in0(and_1_out), .in1(or_1_out), .in2(adder_1_out), .in3(adder_1_out), .out(Result), .sel(ALUOp));  // open: in4, in5, in6, in7

  // Notes on the sheet:
  //   001-OR
  //   000-AND
  //   010-ADD
  //   011-SUB
  //   OR
  //   ADD
  //   Nawal Ayesha Khan 1911301042
  //   AND
  //   SUB
endmodule

module _16_bit_ALU (
  input  B_inv,
  input  [2:0] ALU_Op,
  input  C_In,
  input  [15:0] A,
  input  [15:0] B,
  output [15:0] Result,
  output Zero_Flag,
  output Carry_Out
);

  wire n1_bit_alu_1_carry_out, n1_bit_alu_2_carry_out, n1_bit_alu_3_carry_out, n1_bit_alu_4_carry_out,
       n1_bit_alu_5_carry_out, n1_bit_alu_6_carry_out, n1_bit_alu_7_carry_out, n1_bit_alu_8_carry_out,
       n1_bit_alu_9_carry_out, n1_bit_alu_10_carry_out, n1_bit_alu_11_carry_out, n1_bit_alu_12_carry_out,
       n1_bit_alu_13_carry_out, n1_bit_alu_14_carry_out, n1_bit_alu_15_carry_out;

  _1_bit_ALU u_1_bit_alu_1 (
    .A(A[0]), .B(B[0]), .C_in(C_In), .ALUOp(ALU_Op), .B_In(B_inv), .Result(Result[0]),
    .Carry_Out(n1_bit_alu_1_carry_out));
  _1_bit_ALU u_1_bit_alu_2 (
    .A(A[1]), .B(B[1]), .C_in(n1_bit_alu_1_carry_out), .ALUOp(ALU_Op), .B_In(B_inv), .Result(Result[1]),
    .Carry_Out(n1_bit_alu_2_carry_out));
  _1_bit_ALU u_1_bit_alu_3 (
    .A(A[2]), .B(B[2]), .C_in(n1_bit_alu_2_carry_out), .ALUOp(ALU_Op), .B_In(B_inv), .Result(Result[2]),
    .Carry_Out(n1_bit_alu_3_carry_out));
  _1_bit_ALU u_1_bit_alu_4 (
    .A(A[3]), .B(B[3]), .C_in(n1_bit_alu_3_carry_out), .ALUOp(ALU_Op), .B_In(B_inv), .Result(Result[3]),
    .Carry_Out(n1_bit_alu_4_carry_out));
  _1_bit_ALU u_1_bit_alu_5 (
    .A(A[4]), .B(B[4]), .C_in(n1_bit_alu_4_carry_out), .ALUOp(ALU_Op), .B_In(B_inv), .Result(Result[4]),
    .Carry_Out(n1_bit_alu_5_carry_out));
  _1_bit_ALU u_1_bit_alu_6 (
    .A(A[5]), .B(B[5]), .C_in(n1_bit_alu_5_carry_out), .ALUOp(ALU_Op), .B_In(B_inv), .Result(Result[5]),
    .Carry_Out(n1_bit_alu_6_carry_out));
  _1_bit_ALU u_1_bit_alu_7 (
    .A(A[6]), .B(B[6]), .C_in(n1_bit_alu_6_carry_out), .ALUOp(ALU_Op), .B_In(B_inv), .Result(Result[6]),
    .Carry_Out(n1_bit_alu_7_carry_out));
  _1_bit_ALU u_1_bit_alu_8 (
    .A(A[7]), .B(B[7]), .C_in(n1_bit_alu_7_carry_out), .ALUOp(ALU_Op), .B_In(B_inv), .Result(Result[7]),
    .Carry_Out(n1_bit_alu_8_carry_out));
  _1_bit_ALU u_1_bit_alu_9 (
    .A(A[8]), .B(B[8]), .C_in(n1_bit_alu_8_carry_out), .ALUOp(ALU_Op), .B_In(B_inv), .Result(Result[8]),
    .Carry_Out(n1_bit_alu_9_carry_out));
  _1_bit_ALU u_1_bit_alu_10 (
    .A(A[9]), .B(B[9]), .C_in(n1_bit_alu_9_carry_out), .ALUOp(ALU_Op), .B_In(B_inv), .Result(Result[9]),
    .Carry_Out(n1_bit_alu_10_carry_out));
  _1_bit_ALU u_1_bit_alu_11 (
    .A(A[10]), .B(B[10]), .C_in(n1_bit_alu_10_carry_out), .ALUOp(ALU_Op), .B_In(B_inv), .Result(Result[10]),
    .Carry_Out(n1_bit_alu_11_carry_out));
  _1_bit_ALU u_1_bit_alu_12 (
    .A(A[11]), .B(B[11]), .C_in(n1_bit_alu_11_carry_out), .ALUOp(ALU_Op), .B_In(B_inv), .Result(Result[11]),
    .Carry_Out(n1_bit_alu_12_carry_out));
  _1_bit_ALU u_1_bit_alu_13 (
    .A(A[12]), .B(B[12]), .C_in(n1_bit_alu_12_carry_out), .ALUOp(ALU_Op), .B_In(B_inv), .Result(Result[12]),
    .Carry_Out(n1_bit_alu_13_carry_out));
  _1_bit_ALU u_1_bit_alu_14 (
    .A(A[13]), .B(B[13]), .C_in(n1_bit_alu_13_carry_out), .ALUOp(ALU_Op), .B_In(B_inv), .Result(Result[13]),
    .Carry_Out(n1_bit_alu_14_carry_out));
  _1_bit_ALU u_1_bit_alu_15 (
    .A(A[14]), .B(B[14]), .C_in(n1_bit_alu_14_carry_out), .ALUOp(ALU_Op), .B_In(B_inv), .Result(Result[14]),
    .Carry_Out(n1_bit_alu_15_carry_out));
  _1_bit_ALU u_1_bit_alu_16 (
    .A(A[15]), .B(B[15]), .C_in(n1_bit_alu_15_carry_out), .ALUOp(ALU_Op), .B_In(B_inv), .Result(Result[15]),
    .Carry_Out(Carry_Out));
  nor nor_1 (Zero_Flag, Result[0], Result[1], Result[3], B_inv, Result[4], Result[5], Result[6], Result[7], Result[8], Result[9], Result[10], Result[11], Result[12], Result[13], Result[14], Result[15]);

  // Notes on the sheet:
  //   Nawal Ayesha Khan 1911301042
endmodule

module I_Format_Datapath (
  input  [2:0] ALU_Op,
  input  B_inv,
  input  C_in,
  input  CLK,
  input  RegWrite,
  input  CLR,
  input  MemWrite,
  input  MemRead,
  output [3:0] Opcode,
  output [15:0] out_10,
  output out_11,
  output [15:0] offset
);

  wire [11:0] instruction_fetch_1_instruction;
  wire [15:0] ram_1_data, register_1_read_data_1, register_1_read_data_2;

  Instruction_Fetch instruction_fetch_1 (
    .CLK(CLK), .CLR(CLR), .Instruction({Opcode, instruction_fetch_1_instruction}));  // open: Next_Address
  assign offset = {{12{1'b0}}, instruction_fetch_1_instruction[3:0]};  // Bit_Extender bit_extender_1
  Register register_1 (
    .Write_Register_rd(instruction_fetch_1_instruction[7:4]), .Write_Data(ram_1_data), .RegWrite(RegWrite),
    .CLK(CLK), .Read_data_1(register_1_read_data_1), .Read_data_2(register_1_read_data_2),
    .Read_Register_1_rs(instruction_fetch_1_instruction[11:8]),
    .Read_Register_2__rt(instruction_fetch_1_instruction[7:4]));
  _16_bit_ALU u_16_bit_alu_1 (
    .B_inv(C_in), .ALU_Op(ALU_Op), .C_In(B_inv), .A(register_1_read_data_1), .B(offset), .Result(out_10),
    .Zero_Flag(out_11));  // open: Carry_Out
  RAM #(.addrWidth(16), .dataWidth(16), .bus("separate")) ram_1 (
    .addr(out_10), .din(register_1_read_data_2), .data(ram_1_data), .str(MemWrite), .clk(CLK), .ld(MemRead),
    .clr(CLR));  // open: sel

  // Notes on the sheet:
  //   Nawal Ayesha Khan, 1911301042
  //   rs
  //   rt
  //   immediate
endmodule

module IF_ID_Pipeline_register (
  input  [15:0] Next_Address,
  input  CLK,
  input  CLR,
  input  [15:0] Instruction,
  output [15:0] out_5,
  output [15:0] Instruction_2
);

  Register_part #(.width(16)) register_1 (.D(Next_Address), .Q(out_5), .clk(CLK), .clr(CLR));  // open: en
  Register_part #(.width(16)) register_2 (.D(Instruction), .Q(Instruction_2), .clk(CLK), .clr(CLR));  // open: en
endmodule
