// Logisim project Nawal Ayesha_1911301042 Lab 8.circ as structural Verilog: 2 circuits, main circuit main
module main (
  input  in_1,
  output [1:0] out_2
);

  wire button_1_out, CLK_out;

  Clock CLK (.out(CLK_out));
  _2_bit_Up_Down_Counter u_2_bit_up_down_counter_1 (.CLK(CLK_out), .Q(out_2), .M(in_1), .CLR(button_1_out));
  Button button_1 (.out(button_1_out));
endmodule

module _2_bit_Up_Down_Counter (
  input  M,
  input  CLK,
  input  CLR,
  output [1:0] Q
);

  wire xor_1_out;

  xor xor_1 (xor_1_out, Q[0], M);
  T_Flip_Flop t_ff_1 (.clk(CLK), .T(xor_1_out), .Q(Q[1]), .reset(CLR));  // open: Qn, preset, en
  T_Flip_Flop t_ff_2 (.clk(CLK), .T(1'b1), .Q(Q[0]), .reset(CLR));  // open: Qn, preset, en

  // Notes on the sheet:
  //   Nawal Ayesha Khan, 1911301042
  //   Qb
  //   Qa
endmodule
