// Logisim project Nawal Ayesha_1911301042 Lab Mid Assignment.circ as structural Verilog: 2 circuits, main circuit main
module main (
  input  in_1,
  input  [3:0] in_2,
  input  [3:0] in_3,
  input  [2:0] in_4,
  output [3:0] out_5,
  output out_6
);

  Mid_assignment mid_assignment_1 (.B(in_3), .Carry_In(in_1), .A(in_2), .S(in_4), .Result(out_5), .C_out(out_6));

  // Notes on the sheet:
  //   000:A AND B
  //   001: A OR B
  //   010:A XOR B
  //   011: A'
  //   100, Carry In=0: Add 
  //   101, Carry In=0: Subtract 
  //   110,Carry In=0: Transfer A
  //   110,Carry In=1: Increment A
  //   111, Carry In=1: Transfer A
  //   100, Carry In=1: Add with carry
  //   101, Carry In=1: Subtract with borrow
  //   111, Carry In=0: Decrement A
endmodule

module Mid_assignment (
  input  [3:0] B,
  input  Carry_In,
  input  [3:0] A,
  input  [2:0] S,
  output [3:0] Result,
  output C_out
);

  wire adder_1_cout, adder_1_out, adder_2_cout, adder_2_out, adder_3_cout, adder_3_out, adder_4_out,
       and_1_out, and_2_out, and_3_out, and_4_out, multiplexer_1_out, multiplexer_2_out, multiplexer_3_out,
       multiplexer_4_out, not_1_out, not_2_out, not_3_out, not_4_out, not_5_out, not_6_out, not_7_out,
       not_8_out, or_1_out, or_2_out, or_3_out, or_4_out, xor_1_out, xor_2_out, xor_3_out, xor_4_out;

  and and_1 (and_1_out, B[0], A[0]);
  or or_1 (or_1_out, B[0], A[0]);
  not not_1 (not_1_out, B[0]);
  and and_2 (and_2_out, B[1], A[1]);
  or or_2 (or_2_out, B[1], A[1]);
  not not_2 (not_2_out, B[1]);
  and and_3 (and_3_out, B[2], A[2]);
  or or_3 (or_3_out, B[2], A[2]);
  not not_3 (not_3_out, B[2]);
  and and_4 (and_4_out, B[3], A[3]);
  or or_4 (or_4_out, B[3], A[3]);
  not not_4 (not_4_out, B[3]);
  Multiplexer #(.select(2), .enable("false")) multiplexer_1 (
    .in0(B[0]), .in1(not_1_out), .in2(1'b0), .in3(1'b1), .out(multiplexer_1_out), .sel(S[1:0]));
  Multiplexer #(.select(2), .enable("false")) multiplexer_2 (
    .in0(B[1]), .in1(not_2_out), .in2(1'b0), .in3(1'b1), .out(multiplexer_2_out), .sel(S[1:0]));
  Multiplexer #(.select(2), .enable("false")) multiplexer_3 (
    .in0(B[2]), .in1(not_3_out), .in2(1'b0), .in3(1'b1), .out(multiplexer_3_out), .sel(S[1:0]));
  Multiplexer #(.select(2), .enable("false")) multiplexer_4 (
    .in0(B[3]), .in1(not_4_out), .in2(1'b0), .in3(1'b1), .out(multiplexer_4_out), .sel(S[1:0]));
  xor xor_1 (xor_1_out, B[0], A[0]);
  not not_5 (not_5_out, A[0]);
  Adder #(.width(1)) adder_1 (.a(A[0]), .b(multiplexer_1_out), .out(adder_1_out), .cin(Carry_In), .cout(adder_1_cout));
  xor xor_2 (xor_2_out, B[1], A[1]);
  not not_6 (not_6_out, A[1]);
  Adder #(.width(1)) adder_2 (
    .a(A[1]), .b(multiplexer_2_out), .out(adder_2_out), .cin(adder_1_cout), .cout(adder_2_cout));
  xor xor_3 (xor_3_out, B[2], A[2]);
  not not_7 (not_7_out, A[2]);
  Adder #(.width(1)) adder_3 (
    .a(A[2]), .b(multiplexer_3_out), .out(adder_3_out), .cin(adder_2_cout), .cout(adder_3_cout));
  xor xor_4 (xor_4_out, B[3], A[3]);
  not not_8 (not_8_out, A[3]);
  Adder #(.width(1)) adder_4 (.a(A[3]), .b(multiplexer_4_out), .out(adder_4_out), .cin(adder_3_cout), .cout(C_out));
  Multiplexer #(.select(3), .enable("false")) multiplexer_5 (
    .in0(and_1_out), .in1(or_1_out), .in2(xor_1_out), .in3(not_5_out), .in4(adder_1_out), .in5(adder_1_out),
    .in6(adder_1_out), .in7(adder_1_out), .out(Result[0]), .sel(S));
  Multiplexer #(.select(3), .enable("false")) multiplexer_6 (
    .in0(and_2_out), .in1(or_2_out), .in2(xor_2_out), .in3(not_6_out), .in4(adder_2_out), .in5(adder_2_out),
    .in6(adder_2_out), .in7(adder_2_out), .out(Result[1]), .sel(S));
  Multiplexer #(.select(3), .enable("false")) multiplexer_7 (
    .in0(and_3_out), .in1(or_3_out), .in2(xor_3_out), .in3(not_7_out), .in4(adder_3_out), .in5(adder_3_out),
    .in6(adder_3_out), .in7(adder_3_out), .out(Result[2]), .sel(S));
  Multiplexer #(.select(3), .enable("false")) multiplexer_8 (
    .in0(and_4_out), .in1(or_4_out), .in2(xor_4_out), .in3(not_8_out), .in4(adder_4_out), .in5(adder_4_out),
    .in6(adder_4_out), .in7(adder_4_out), .out(Result[3]), .sel(S));

  // Notes on the sheet:
  //   000:A AND B
  //   001: A OR B
  //   010:A XOR B
  //   011: A'
  //   100, Carry In=0: Add 
  //   101, Carry In=0: Subtract 
  //   100, Carry In=1: Add with carry
  //   101, Carry In=1: Subtract with borrow
  //   110,Carry In=0: Transfer A
  //   110,Carry In=1: Increment A
  //   111, Carry In=0: Decrement A
  //   111, Carry In=1: Transfer A
  //   Nawal Ayesha Khan, 1911301042
  //   D0
  //   D1
  //   D2
  //   D3
endmodule
