// Logisim project Nawal Ayesha_1911301042 Mid Q3.circ as structural Verilog
module main (
  input  in_1,
  input  in_2,
  output [1:0] out_3,
  output [12:0] out_4,
  output [12:0] out_5,
  output [12:0] out_6,
  output [12:0] out_7,
  output [12:0] out_8,
  output [2:0] out_9,
  output [2:0] out_10,
  output [2:0] out_11,
  output [2:0] out_12,
  output [1:0] out_13
);

  wire and_1_out, CLK_out, ex_1_out_11, instruction_control_1_aluop0, instruction_control_1_aluop1,
       instruction_control_1_alusrc, instruction_control_1_branch, instruction_control_1_memread,
       instruction_control_1_memtoreg, instruction_control_1_memwrite, instruction_control_1_regdst,
       instruction_control_1_regwrite;
  wire [12:0] ex_1_address, instruction_decode_1_offset, instruction_fetch_1_next_instruction,
       mem_1_read_data;

  Clock CLK (.out(CLK_out));
  Instruction_Fetch instruction_fetch_1 (
    .CLR(in_2), .CLK(CLK_out), .out_6({out_3, out_7[10:0]}), .Branch_address(ex_1_address),
    .PCSrc(and_1_out), .Next_instruction(instruction_fetch_1_next_instruction));
  Instruction_Control instruction_control_1 (
    .Opcode(out_3), .RegDst(instruction_control_1_regdst), .ALUSrc(instruction_control_1_alusrc),
    .MemtoReg(instruction_control_1_memtoreg), .RegWrite(instruction_control_1_regwrite),
    .MemRead(instruction_control_1_memread), .MemWrite(instruction_control_1_memwrite),
    .Branch(instruction_control_1_branch), .ALUOp1(instruction_control_1_aluop1),
    .ALUOp0(instruction_control_1_aluop0));
  Instruction_Decode instruction_decode_1 (
    .rs(out_7[10:8]), .rt(out_7[7:5]), .rd(out_7[4:2]), .in_4(out_6), .CLK(CLK_out), .funct(out_7[1:0]),
    .out_9(out_8), .RegDst(instruction_control_1_regdst), .offset(instruction_decode_1_offset),
    .REGWR(instruction_control_1_regwrite), .out_10(out_4));
  EX ex_1 (
    .Next_address(instruction_fetch_1_next_instruction), .in_2(in_1), .in_3(in_1), .in_4(out_12),
    .in_5(in_1), .Read_reg_1(out_8), .Read_reg_2(out_4), .Offset(instruction_decode_1_offset),
    .ALUSrc(instruction_control_1_alusrc), .Address(ex_1_address), .out_11(ex_1_out_11), .out_12(out_5));  // open: out_13, out_14
  ALU_Control_2 alu_control_2_1 (
    .out_5(out_12), .B(instruction_control_1_aluop1), .A(instruction_control_1_aluop0), .F1(out_7[1]),
    .F0(out_7[0]));
  and and_1 (and_1_out, ex_1_out_11, instruction_control_1_branch);
  MEM mem_1 (
    .Address(out_5), .Write_Data(out_4), .MemWrite(instruction_control_1_memwrite), .CLK(CLK_out),
    .Read_Data(mem_1_read_data), .MemRead(instruction_control_1_memread));
  Multiplexer #(.width(13), .enable("false")) multiplexer_1 (
    .in0(out_5), .in1(mem_1_read_data), .out(out_6), .sel(instruction_control_1_memtoreg));

  assign out_7[12:11] = out_3;
  assign out_9 = out_7[10:8];
  assign out_10 = out_7[7:5];
  assign out_11 = out_7[4:2];
  assign out_13 = out_7[1:0];
endmodule

module _1_bit_ALU (
  input  [2:0] AluOp,
  input  A_invert,
  input  B_invert,
  input  C_in,
  input  A,
  input  B,
  output Result,
  output Carry_Out
);

  wire adder_1_out, and_1_out, multiplexer_1_out, multiplexer_2_out, not_1_out, not_2_out, or_1_out;

  not not_1 (not_1_out, A);
  not not_2 (not_2_out, B);
  Multiplexer #(.enable("false")) multiplexer_1 (.in0(A), .in1(not_1_out), .out(multiplexer_1_out), .sel(A_invert));
  Multiplexer #(.enable("false")) multiplexer_2 (.in0(B), .in1(not_2_out), .out(multiplexer_2_out), .sel(B_invert));
  and and_1 (and_1_out, multiplexer_1_out, multiplexer_2_out);
  or or_1 (or_1_out, multiplexer_1_out, multiplexer_2_out);
  Adder #(.width(1)) adder_1 (
    .a(multiplexer_1_out), .b(multiplexer_2_out), .out(adder_1_out), .cin(C_in), .cout(Carry_Out));
  Multiplexer #(.select(3), .enable("false")) multiplexer_3 (
    .in0(and_1_out), .in1(or_1_out), .in2(adder_1_out), .in3(or_1_out), .in4(and_1_out), .in6(adder_1_out),
    .in7(and_1_out), .out(Result), .sel(AluOp));  // open: in5
endmodule

module _13_bit_Multiplier (
  input  [12:0] A,
  input  [12:0] B,
  output [12:0] Product_S,
  output Mult_zero_flag
);

  wire or_1_out;
  wire [7:5] n4_bit_multiplier_2_s;

  _4_bit_Multiplier u_4_bit_multiplier_1 (.A(A[3:0]), .B(B[3:0]), .S(Product_S[7:0]));
  _4_bit_Multiplier u_4_bit_multiplier_2 (.A(A[7:4]), .B(B[7:4]), .S({n4_bit_multiplier_2_s, Product_S[12:8]}));
  or or_1 (or_1_out, Product_S[0], Product_S[1], Product_S[2], Product_S[3], Product_S[4], Product_S[5], Product_S[6], Product_S[7], Product_S[8], Product_S[9], Product_S[10], Product_S[11], Product_S[12]);
  not not_1 (Mult_zero_flag, or_1_out);
endmodule

module _4_bit_Multiplier (
  input  [3:0] A,
  input  [3:0] B,
  output [7:0] S
);

  wire [2:0] and_2_out;
  wire [3:0] and_5_out, and_9_out, and_13_out;
  wire [3:1] adder_1_out, adder_2_out;
  wire [3:3] adder_1_cout, adder_2_cout;

  and and_1 (S[0], A[0], B[0]);
  and and_2 (and_2_out[0], A[0], B[1]);
  and and_3 (and_2_out[1], A[0], B[2]);
  and and_4 (and_2_out[2], A[0], B[3]);
  and and_5 (and_5_out[0], A[1], B[0]);
  and and_6 (and_5_out[1], A[1], B[1]);
  and and_7 (and_5_out[2], A[1], B[2]);
  and and_8 (and_5_out[3], A[1], B[3]);
  Adder #(.width(4)) adder_1 (
    .a({1'b0, and_2_out}), .b(and_5_out), .out({adder_1_out, S[1]}), .cin(1'b0), .cout(adder_1_cout[3]));
  and and_9 (and_9_out[0], A[2], B[0]);
  and and_10 (and_9_out[1], A[2], B[1]);
  and and_11 (and_9_out[2], A[2], B[2]);
  and and_12 (and_9_out[3], A[2], B[3]);
  Adder #(.width(4)) adder_2 (
    .a({adder_1_cout[3], adder_1_out}), .b(and_9_out), .out({adder_2_out, S[2]}), .cin(1'b0),
    .cout(adder_2_cout[3]));
  and and_13 (and_13_out[0], A[3], B[0]);
  and and_14 (and_13_out[1], A[3], B[1]);
  and and_15 (and_13_out[2], A[3], B[2]);
  and and_16 (and_13_out[3], A[3], B[3]);
  Adder #(.width(4)) adder_3 (
    .a({adder_2_cout[3], adder_2_out}), .b(and_13_out), .out(S[6:3]), .cin(1'b0), .cout(S[7]));

  // Notes on the sheet:
  //   A1B1
  //   A1B2
  //   A1B3
  //   A1B4
  //   A2B1
  //   A2B2
  //   A2B3
  //   A2B4
  //   A3B1
  //   A3B2
  //   A3B3
  //   A3B4
  //   A4B1
  //   A4B2
  //   A4B3
  //   A4B4
endmodule

module _13_bit_ALU (
  input  [2:0] ALU_Op,
  input  C_in,
  input  B_inv,
  input  A_inv,
  input  [12:0] A,
  input  [12:0] B,
  output [12:0] Result,
  output Zero_Flag,
  output Overflow,
  output Carry_Out
);

  wire n1_bit_alu_1_carry_out, n1_bit_alu_2_carry_out, n1_bit_alu_3_carry_out, n1_bit_alu_4_carry_out,
       n1_bit_alu_5_carry_out, n1_bit_alu_6_carry_out, n1_bit_alu_7_carry_out, n1_bit_alu_8_carry_out,
       n1_bit_alu_9_carry_out, n1_bit_alu_10_carry_out, n1_bit_alu_11_carry_out, n1_bit_alu_12_carry_out,
       n13_bit_multiplier_1_mult_zero_flag, not_1_out, or_1_out;
  wire [12:0] n1_bit_alu_1_result, n13_bit_multiplier_1_product_s;

  _1_bit_ALU u_1_bit_alu_1 (
    .Result(n1_bit_alu_1_result[0]), .Carry_Out(n1_bit_alu_1_carry_out), .A(A[0]), .B(B[0]),
    .A_invert(A_inv), .B_invert(B_inv), .AluOp(ALU_Op), .C_in(C_in));
  _1_bit_ALU u_1_bit_alu_2 (
    .Result(n1_bit_alu_1_result[1]), .Carry_Out(n1_bit_alu_2_carry_out), .A(A[1]), .B(B[1]),
    .A_invert(A_inv), .B_invert(B_inv), .AluOp(ALU_Op), .C_in(n1_bit_alu_1_carry_out));
  _1_bit_ALU u_1_bit_alu_3 (
    .Result(n1_bit_alu_1_result[2]), .Carry_Out(n1_bit_alu_3_carry_out), .A(A[2]), .B(B[2]),
    .A_invert(A_inv), .B_invert(B_inv), .AluOp(ALU_Op), .C_in(n1_bit_alu_2_carry_out));
  _1_bit_ALU u_1_bit_alu_4 (
    .Result(n1_bit_alu_1_result[3]), .Carry_Out(n1_bit_alu_4_carry_out), .A(A[3]), .B(B[3]),
    .A_invert(A_inv), .B_invert(B_inv), .AluOp(ALU_Op), .C_in(n1_bit_alu_3_carry_out));
  _1_bit_ALU u_1_bit_alu_5 (
    .Result(n1_bit_alu_1_result[4]), .Carry_Out(n1_bit_alu_5_carry_out), .A(A[4]), .B(B[4]),
    .A_invert(A_inv), .B_invert(B_inv), .AluOp(ALU_Op), .C_in(n1_bit_alu_4_carry_out));
  _1_bit_ALU u_1_bit_alu_6 (
    .Result(n1_bit_alu_1_result[5]), .Carry_Out(n1_bit_alu_6_carry_out), .A(A[5]), .B(B[5]),
    .A_invert(A_inv), .B_invert(B_inv), .AluOp(ALU_Op), .C_in(n1_bit_alu_5_carry_out));
  _1_bit_ALU u_1_bit_alu_7 (
    .Result(n1_bit_alu_1_result[6]), .Carry_Out(n1_bit_alu_7_carry_out), .A(A[6]), .B(B[6]),
    .A_invert(A_inv), .B_invert(B_inv), .AluOp(ALU_Op), .C_in(n1_bit_alu_6_carry_out));
  _1_bit_ALU u_1_bit_alu_8 (
    .Result(n1_bit_alu_1_result[7]), .Carry_Out(n1_bit_alu_8_carry_out), .A(A[7]), .B(B[7]),
    .A_invert(A_inv), .B_invert(B_inv), .AluOp(ALU_Op), .C_in(n1_bit_alu_7_carry_out));
  _1_bit_ALU u_1_bit_alu_9 (
    .Result(n1_bit_alu_1_result[8]), .Carry_Out(n1_bit_alu_9_carry_out), .A(A[8]), .B(B[8]),
    .A_invert(A_inv), .B_invert(B_inv), .AluOp(ALU_Op), .C_in(n1_bit_alu_8_carry_out));
  _1_bit_ALU u_1_bit_alu_10 (
    .Result(n1_bit_alu_1_result[9]), .Carry_Out(n1_bit_alu_10_carry_out), .A(A[9]), .B(B[9]),
    .A_invert(A_inv), .B_invert(B_inv), .AluOp(ALU_Op), .C_in(n1_bit_alu_9_carry_out));
  _1_bit_ALU u_1_bit_alu_11 (
    .Result(n1_bit_alu_1_result[10]), .Carry_Out(n1_bit_alu_11_carry_out), .A(A[10]), .B(B[10]),
    .A_invert(A_inv), .B_invert(B_inv), .AluOp(ALU_Op), .C_in(n1_bit_alu_10_carry_out));
  _1_bit_ALU u_1_bit_alu_12 (
    .Result(n1_bit_alu_1_result[11]), .Carry_Out(n1_bit_alu_12_carry_out), .A(A[11]), .B(B[11]),
    .A_invert(A_inv), .B_invert(B_inv), .AluOp(ALU_Op), .C_in(n1_bit_alu_11_carry_out));
  _1_bit_ALU u_1_bit_alu_13 (
    .Result(n1_bit_alu_1_result[12]), .Carry_Out(Carry_Out), .A(A[12]), .B(B[12]), .A_invert(A_inv),
    .B_invert(B_inv), .AluOp(ALU_Op), .C_in(n1_bit_alu_12_carry_out));
  _13_bit_Multiplier u_13_bit_multiplier_1 (
    .A(A), .B(B), .Product_S(n13_bit_multiplier_1_product_s),
    .Mult_zero_flag(n13_bit_multiplier_1_mult_zero_flag));
  Multiplexer #(.select(3), .width(13), .enable("false")) multiplexer_1 (
    .in0(n1_bit_alu_1_result), .in1(n1_bit_alu_1_result), .in2(n1_bit_alu_1_result),
    .in3(n1_bit_alu_1_result), .in4(n1_bit_alu_1_result), .in6(n1_bit_alu_1_result),
    .in7(n13_bit_multiplier_1_product_s), .out(Result), .sel(ALU_Op));  // open: in5
  or or_1 (or_1_out, n1_bit_alu_1_result[0], n1_bit_alu_1_result[1], n1_bit_alu_1_result[2], n1_bit_alu_1_result[3], n1_bit_alu_1_result[4], n1_bit_alu_1_result[5], n1_bit_alu_1_result[6], n1_bit_alu_1_result[7], n1_bit_alu_1_result[8], n1_bit_alu_1_result[9], n1_bit_alu_1_result[10], n1_bit_alu_1_result[11], n1_bit_alu_1_result[12]);
  xor xor_1 (Overflow, n1_bit_alu_12_carry_out, Carry_Out);
  not not_1 (not_1_out, or_1_out);
  Multiplexer #(.select(3), .enable("false")) multiplexer_2 (
    .in0(not_1_out), .in1(not_1_out), .in2(not_1_out), .in3(not_1_out), .in4(not_1_out), .in6(not_1_out),
    .in7(n13_bit_multiplier_1_mult_zero_flag), .out(Zero_Flag), .sel(ALU_Op));  // open: in5
endmodule

module Instruction_Fetch (
  input  [12:0] Branch_address,
  input  CLK,
  input  PCSrc,
  input  CLR,
  output [12:0] Next_instruction,
  output [12:0] out_6
);

  wire [12:0] multiplexer_1_out, register_1_q;

  Multiplexer #(.width(13), .enable("false")) multiplexer_1 (
    .in0(Next_instruction), .in1(Branch_address), .out(multiplexer_1_out), .sel(PCSrc));
  Register #(.width(13)) register_1 (.D(multiplexer_1_out), .en(1'b1), .Q(register_1_q), .clk(CLK), .clr(CLR));
  ROM #(.addrWidth(13), .dataWidth(13)) rom_1 (.addr(register_1_q), .data(out_6));  // open: sel
  Adder #(.width(13)) adder_1 (.a(13'h1), .b(register_1_q), .out(Next_instruction), .cin(1'b0));  // open: cout

  // Notes on the sheet:
  //   PC
  //   Address
  //   contents of rom_1 (hex, n*v repeats v):
  //   800 4 8 1900 228 1044 1d1 111 11 10 43 1001 1010 1011 1110 101
  //   Instruction
endmodule

module Instruction_Control (
  input  [1:0] Opcode,
  output RegDst,
  output ALUSrc,
  output MemtoReg,
  output RegWrite,
  output MemRead,
  output MemWrite,
  output Branch,
  output ALUOp1,
  output ALUOp0
);

  wire not_1_out, not_2_out;

  not not_1 (not_1_out, Opcode[0]);
  not not_2 (not_2_out, Opcode[1]);
  and and_1 (ALUOp1, not_1_out, not_2_out);
  and and_2 (MemRead, not_2_out, Opcode[0]);
  and and_3 (MemWrite, not_1_out, Opcode[1]);
  and and_4 (ALUOp0, Opcode[0], Opcode[1]);
  or or_1 (ALUSrc, MemRead, MemWrite);
  or or_2 (RegWrite, ALUOp1, MemRead);

  assign Branch = ALUOp0;
  assign MemtoReg = MemRead;
  assign RegDst = ALUOp1;

  // Notes on the sheet:
  //   R-Format
  //   lw
  //   sw
  //   beq
endmodule

module ALU_Control_2 (
  input  B,
  input  A,
  input  F1,
  input  F0,
  output [2:0] out_5
);

  wire not_1_out, not_2_out;

  not not_1 (not_1_out, A);
  not not_2 (not_2_out, F0);
  and and_1 (out_5[2], not_2_out, F1, not_1_out, B);
  and and_2 (out_5[1], B, not_1_out, not_2_out);
  and and_3 (out_5[0], F0, F1, not_1_out, B);
endmodule

module Instruction_Decode (
  input  [2:0] rs,
  input  [2:0] rt,
  input  [2:0] rd,
  input  [12:0] in_4,
  input  RegDst,
  input  CLK,
  input  REGWR,
  input  [1:0] funct,
  output [12:0] out_9,
  output [12:0] out_10,
  output [12:0] offset
);

  wire [2:0] multiplexer_1_out;

  Multiplexer #(.width(3), .enable("false")) multiplexer_1 (.in0(rt), .in1(rd), .out(multiplexer_1_out), .sel(RegDst));
  assign offset = {{8{1'b0}}, {rd, funct}};  // Bit_Extender bit_extender_1
  Register_file_main main_1 (
    .WriteData(in_4), .Write_Register(multiplexer_1_out), .RegWrite(REGWR), .Read_data_1(out_9),
    .Read_register_1__rs(rs), .Read_data_2(out_10), .Read_register_2__rt(rt), .clk(CLK));
endmodule

module EX (
  input  [12:0] Next_address,
  input  in_2,
  input  in_3,
  input  [2:0] in_4,
  input  in_5,
  input  [12:0] Read_reg_1,
  input  [12:0] Read_reg_2,
  input  [12:0] Offset,
  input  ALUSrc,
  output [12:0] Address,
  output out_11,
  output [12:0] out_12,
  output out_13,
  output out_14
);

  wire [12:0] multiplexer_1_out, shifter_1_out;

  Multiplexer #(.width(13), .enable("false")) multiplexer_1 (
    .in0(Read_reg_2), .in1(Offset), .out(multiplexer_1_out), .sel(ALUSrc));
  Shifter #(.width(13)) shifter_1 (.in(Offset), .\dist (4'b0010), .out(shifter_1_out));
  _13_bit_ALU u_13_bit_alu_1 (
    .C_in(in_2), .B_inv(in_3), .A_inv(in_5), .A(Read_reg_1), .B(multiplexer_1_out), .Result(out_12),
    .Zero_Flag(out_11), .ALU_Op(in_4), .Carry_Out(out_14), .Overflow(out_13));
  Adder #(.width(13)) adder_1 (.a(Next_address), .b(shifter_1_out), .out(Address), .cin(1'b0));  // open: cout
endmodule

module MEM (
  input  [12:0] Address,
  input  [12:0] Write_Data,
  input  MemWrite,
  input  MemRead,
  input  CLK,
  output [12:0] Read_Data
);

  RAM #(.addrWidth(13), .dataWidth(13), .bus("separate")) ram_1 (
    .addr(Address), .din(Write_Data), .data(Read_Data), .str(MemWrite), .clk(CLK), .ld(MemRead));  // open: sel, clr
endmodule

module pp (
  input  [2:0] in_1,
  input  [2:0] in_2,
  input  [2:0] in_3,
  input  [2:0] in_4,
  input  in_5,
  input  [1:0] in_6,
  input  [12:0] in_7,
  input  [12:0] in_8,
  input  [12:0] in_9,
  input  in_10,
  input  in_11,
  input  in_12,
  input  [12:0] in_13,
  input  [12:0] in_14,
  input  [2:0] in_15,
  input  [2:0] in_16,
  input  in_17,
  input  in_18,
  input  in_19,
  input  in_20,
  input  [2:0] in_21,
  input  [12:0] in_22,
  output [12:0] out_23,
  output [12:0] out_24,
  output [12:0] out_25,
  output [12:0] out_26,
  output [12:0] out_27
);

  Instruction_Decode instruction_decode_1 (
    .rs(in_1), .rt(in_2), .rd(in_4), .in_4(in_7), .CLK(in_12), .funct(in_6), .out_9(out_23), .RegDst(in_11),
    .REGWR(in_10), .out_10(out_24));  // open: offset
  Register_file_main main_1 (
    .WriteData(in_22), .Write_Register(in_21), .RegWrite(in_10), .Read_data_1(out_23),
    .Read_register_1__rs(in_15), .Read_data_2(out_24), .Read_register_2__rt(in_16), .clk(in_12));
  EX ex_1 (
    .Next_address(in_8), .in_2(in_5), .in_3(in_5), .in_4(in_3), .in_5(in_5), .Read_reg_1(in_9),
    .Read_reg_2(in_13), .Offset(in_14), .ALUSrc(in_17), .Address(out_25), .out_12(out_27));  // open: out_11, out_13, out_14
  MEM mem_1 (.Address(out_25), .Write_Data(out_27), .MemWrite(in_19), .CLK(in_18), .Read_Data(out_26), .MemRead(in_20));
endmodule
