// Logisim project Nawal Ayesha_1911301042 Project.circ as structural Verilog: 15 circuits, main circuit main
module main (
  input  in_1,
  output [12:0] out_2,
  output [12:0] out_3,
  output [12:0] out_4,
  output [1:0] op,
  output [12:0] out_6,
  output [12:0] out_7,
  output [12:0] out_8,
  output [2:0] out_9,
  output [12:0] out_10,
  output [2:0] out_11,
  output [12:0] out_12,
  output [2:0] out_13,
  output [1:0] funct,
  output [12:0] out_15,
  output [12:0] out_16,
  output [2:0] out_17
);

  wire and_1_out, CLK_out, ex_1_out_8, instruction_control_new_1_alusrc, instruction_control_new_1_branch,
       instruction_control_new_1_memread, instruction_control_new_1_memtoreg,
       instruction_control_new_1_memwrite, instruction_control_new_1_regdst,
       instruction_control_new_1_regwrite;
  wire [1:0] instruction_control_new_1_aluop;
  wire [2:2] nor_1_out;

  Clock CLK (.out(CLK_out));
  Instruction_Fetch instruction_fetch_1 (
    .CLR(in_1), .CLK(CLK_out), .Instruction({op, out_8[10:2], funct}), .Branch_address(out_2),
    .PCSrc(and_1_out), .Next_instruction(out_4));
  nor nor_1 (nor_1_out[2], op[0], op[1]);
  Instruction_Control_new instruction_control_new_1 (
    .Opcode({nor_1_out[2], op}), .RegDst(instruction_control_new_1_regdst),
    .RegWrite(instruction_control_new_1_regwrite), .ALUSrc(instruction_control_new_1_alusrc),
    .MemRead(instruction_control_new_1_memread), .MemWrite(instruction_control_new_1_memwrite),
    .MemtoReg(instruction_control_new_1_memtoreg), .Branch(instruction_control_new_1_branch),
    .ALUOp(instruction_control_new_1_aluop));
  Instruction_Decode instruction_decode_1 (
    .rs(out_8[10:8]), .rt(out_8[7:5]), .rd(out_8[4:2]), .in_4(out_7), .CLK(CLK_out), .funct(funct),
    .out_9(out_10), .RegDst(instruction_control_new_1_regdst), .offset(out_15),
    .REGWR(instruction_control_new_1_regwrite), .out_10(out_6));
  EX ex_1 (
    .Next_address(out_4), ._010(out_17), .Read_reg_1(out_10), .Read_reg_2(out_6), .Offset(out_15),
    .ALUSrc(instruction_control_new_1_alusrc), .Address(out_2), .out_8(ex_1_out_8), ._7(out_3));  // open: out_10, out_11
  ALU_Control alu_control_1 (
    .out_5(out_17), .B(instruction_control_new_1_aluop[1]), .A(instruction_control_new_1_aluop[0]),
    .F1(funct[1]), .F0(funct[0]));
  and and_1 (and_1_out, ex_1_out_8, instruction_control_new_1_branch);
  MEM mem_1 (
    .Address(out_3), .Write_Data(out_6), .MemWrite(instruction_control_new_1_memwrite), .CLK(CLK_out),
    .Read_Data(out_16), .MemRead(instruction_control_new_1_memread));
  WB wb_1 (.Result(out_3), .Read_Data(out_16), .MemToReg(instruction_control_new_1_memtoreg), ._7(out_7));

  assign {out_8[12:11], out_8[1:0]} = {op, funct};
  assign out_9 = out_8[10:8];
  assign out_11 = out_8[7:5];
  assign out_12 = out_6;
  assign out_13 = out_8[4:2];
endmodule

module _1_bit_ALU (
  input  [2:0] AluOp,
  input  A_invert,
  input  B_invert,
  input  C_in,
  input  A,
  input  B,
  output Result,
  output Carry_Out
);

  wire adder_1_out, and_1_out, multiplexer_1_out, multiplexer_2_out, not_1_out, not_2_out, or_1_out;

  not not_1 (not_1_out, A);
  not not_2 (not_2_out, B);
  Multiplexer #(.enable("false")) multiplexer_1 (.in0(A), .in1(not_1_out), .out(multiplexer_1_out), .sel(A_invert));
  Multiplexer #(.enable("false")) multiplexer_2 (.in0(B), .in1(not_2_out), .out(multiplexer_2_out), .sel(B_invert));
  and and_1 (and_1_out, multiplexer_1_out, multiplexer_2_out);
  or or_1 (or_1_out, multiplexer_1_out, multiplexer_2_out);
  Adder #(.width(1)) adder_1 (
    .a(multiplexer_1_out), .b(multiplexer_2_out), .out(adder_1_out), .cin(C_in), .cout(Carry_Out));
  Multiplexer #(.select(3), .enable("false")) multiplexer_3 (
    .in0(and_1_out), .in1(or_1_out), .in2(adder_1_out), .in3(or_1_out), .in4(and_1_out), .in6(adder_1_out),
    .in7(and_1_out), .out(Result), .sel(AluOp));  // open: in5
endmodule

module _13_bit_Multiplier (
  input  [12:0] A,
  input  [12:0] B,
  output [12:0] Product_S,
  output Mult_zero_flag
);

  wire or_1_out;
  wire [7:5] n4_bit_multiplier_2_s;

  _4_bit_Multiplier u_4_bit_multiplier_1 (.A(A[3:0]), .B(B[3:0]), .S(Product_S[7:0]));
  _4_bit_Multiplier u_4_bit_multiplier_2 (.A(A[7:4]), .B(B[7:4]), .S({n4_bit_multiplier_2_s, Product_S[12:8]}));
  or or_1 (or_1_out, Product_S[0], Product_S[1], Product_S[2], Product_S[3], Product_S[4], Product_S[5], Product_S[6], Product_S[7], Product_S[8], Product_S[9], Product_S[10], Product_S[11], Product_S[12]);
  not not_1 (Mult_zero_flag, or_1_out);
endmodule

module _4_bit_Multiplier (
  input  [3:0] A,
  input  [3:0] B,
  output [7:0] S
);

  wire [2:0] and_2_out;
  wire [3:0] and_5_out, and_9_out, and_13_out;
  wire [3:1] adder_1_out, adder_2_out;
  wire [3:3] adder_1_cout, adder_2_cout;

  and and_1 (S[0], A[0], B[0]);
  and and_2 (and_2_out[0], A[0], B[1]);
  and and_3 (and_2_out[1], A[0], B[2]);
  and and_4 (and_2_out[2], A[0], B[3]);
  and and_5 (and_5_out[0], A[1], B[0]);
  and and_6 (and_5_out[1], A[1], B[1]);
  and and_7 (and_5_out[2], A[1], B[2]);
  and and_8 (and_5_out[3], A[1], B[3]);
  Adder #(.width(4)) adder_1 (
    .a({1'b0, and_2_out}), .b(and_5_out), .out({adder_1_out, S[1]}), .cin(1'b0), .cout(adder_1_cout[3]));
  and and_9 (and_9_out[0], A[2], B[0]);
  and and_10 (and_9_out[1], A[2], B[1]);
  and and_11 (and_9_out[2], A[2], B[2]);
  and and_12 (and_9_out[3], A[2], B[3]);
  Adder #(.width(4)) adder_2 (
    .a({adder_1_cout[3], adder_1_out}), .b(and_9_out), .out({adder_2_out, S[2]}), .cin(1'b0),
    .cout(adder_2_cout[3]));
  and and_13 (and_13_out[0], A[3], B[0]);
  and and_14 (and_13_out[1], A[3], B[1]);
  and and_15 (and_13_out[2], A[3], B[2]);
  and and_16 (and_13_out[3], A[3], B[3]);
  Adder #(.width(4)) adder_3 (
    .a({adder_2_cout[3], adder_2_out}), .b(and_13_out), .out(S[6:3]), .cin(1'b0), .cout(S[7]));

  // Notes on the sheet:
  //   A1B1
  //   A1B2
  //   A1B3
  //   A1B4
  //   A2B1
  //   A2B2
  //   A2B3
  //   A2B4
  //   A3B1
  //   A3B2
  //   A3B3
  //   A3B4
  //   A4B1
  //   A4B2
  //   A4B3
  //   A4B4
endmodule

module _13_bit_ALU (
  input  [2:0] ALU_Op,
  input  C_in,
  input  B_inv,
  input  A_inv,
  input  [12:0] A,
  input  [12:0] B,
  output [12:0] Result,
  output Zero_Flag,
  output Overflow,
  output Carry_Out
);

  wire n1_bit_alu_1_carry_out, n1_bit_alu_2_carry_out, n1_bit_alu_3_carry_out, n1_bit_alu_4_carry_out,
       n1_bit_alu_5_carry_out, n1_bit_alu_6_carry_out, n1_bit_alu_7_carry_out, n1_bit_alu_8_carry_out,
       n1_bit_alu_9_carry_out, n1_bit_alu_10_carry_out, n1_bit_alu_11_carry_out, n1_bit_alu_12_carry_out,
       n13_bit_multiplier_1_mult_zero_flag, not_1_out, or_1_out;
  wire [12:0] n1_bit_alu_1_result, n13_bit_multiplier_1_product_s;

  _1_bit_ALU u_1_bit_alu_1 (
    .Result(n1_bit_alu_1_result[0]), .Carry_Out(n1_bit_alu_1_carry_out), .A(A[0]), .B(B[0]),
    .A_invert(A_inv), .B_invert(B_inv), .AluOp(ALU_Op), .C_in(C_in));
  _1_bit_ALU u_1_bit_alu_2 (
    .Result(n1_bit_alu_1_result[1]), .Carry_Out(n1_bit_alu_2_carry_out), .A(A[1]), .B(B[1]),
    .A_invert(A_inv), .B_invert(B_inv), .AluOp(ALU_Op), .C_in(n1_bit_alu_1_carry_out));
  _1_bit_ALU u_1_bit_alu_3 (
    .Result(n1_bit_alu_1_result[2]), .Carry_Out(n1_bit_alu_3_carry_out), .A(A[2]), .B(B[2]),
    .A_invert(A_inv), .B_invert(B_inv), .AluOp(ALU_Op), .C_in(n1_bit_alu_2_carry_out));
  _1_bit_ALU u_1_bit_alu_4 (
    .Result(n1_bit_alu_1_result[3]), .Carry_Out(n1_bit_alu_4_carry_out), .A(A[3]), .B(B[3]),
    .A_invert(A_inv), .B_invert(B_inv), .AluOp(ALU_Op), .C_in(n1_bit_alu_3_carry_out));
  _1_bit_ALU u_1_bit_alu_5 (
    .Result(n1_bit_alu_1_result[4]), .Carry_Out(n1_bit_alu_5_carry_out), .A(A[4]), .B(B[4]),
    .A_invert(A_inv), .B_invert(B_inv), .AluOp(ALU_Op), .C_in(n1_bit_alu_4_carry_out));
  _1_bit_ALU u_1_bit_alu_6 (
    .Result(n1_bit_alu_1_result[5]), .Carry_Out(n1_bit_alu_6_carry_out), .A(A[5]), .B(B[5]),
    .A_invert(A_inv), .B_invert(B_inv), .AluOp(ALU_Op), .C_in(n1_bit_alu_5_carry_out));
  _1_bit_ALU u_1_bit_alu_7 (
    .Result(n1_bit_alu_1_result[6]), .Carry_Out(n1_bit_alu_7_carry_out), .A(A[6]), .B(B[6]),
    .A_invert(A_inv), .B_invert(B_inv), .AluOp(ALU_Op), .C_in(n1_bit_alu_6_carry_out));
  _1_bit_ALU u_1_bit_alu_8 (
    .Result(n1_bit_alu_1_result[7]), .Carry_Out(n1_bit_alu_8_carry_out), .A(A[7]), .B(B[7]),
    .A_invert(A_inv), .B_invert(B_inv), .AluOp(ALU_Op), .C_in(n1_bit_alu_7_carry_out));
  _1_bit_ALU u_1_bit_alu_9 (
    .Result(n1_bit_alu_1_result[8]), .Carry_Out(n1_bit_alu_9_carry_out), .A(A[8]), .B(B[8]),
    .A_invert(A_inv), .B_invert(B_inv), .AluOp(ALU_Op), .C_in(n1_bit_alu_8_carry_out));
  _1_bit_ALU u_1_bit_alu_10 (
    .Result(n1_bit_alu_1_result[9]), .Carry_Out(n1_bit_alu_10_carry_out), .A(A[9]), .B(B[9]),
    .A_invert(A_inv), .B_invert(B_inv), .AluOp(ALU_Op), .C_in(n1_bit_alu_9_carry_out));
  _1_bit_ALU u_1_bit_alu_11 (
    .Result(n1_bit_alu_1_result[10]), .Carry_Out(n1_bit_alu_11_carry_out), .A(A[10]), .B(B[10]),
    .A_invert(A_inv), .B_invert(B_inv), .AluOp(ALU_Op), .C_in(n1_bit_alu_10_carry_out));
  _1_bit_ALU u_1_bit_alu_12 (
    .Result(n1_bit_alu_1_result[11]), .Carry_Out(n1_bit_alu_12_carry_out), .A(A[11]), .B(B[11]),
    .A_invert(A_inv), .B_invert(B_inv), .AluOp(ALU_Op), .C_in(n1_bit_alu_11_carry_out));
  _1_bit_ALU u_1_bit_alu_13 (
    .Result(n1_bit_alu_1_result[12]), .Carry_Out(Carry_Out), .A(A[12]), .B(B[12]), .A_invert(A_inv),
    .B_invert(B_inv), .AluOp(ALU_Op), .C_in(n1_bit_alu_12_carry_out));
  _13_bit_Multiplier u_13_bit_multiplier_1 (
    .A(A), .B(B), .Product_S(n13_bit_multiplier_1_product_s),
    .Mult_zero_flag(n13_bit_multiplier_1_mult_zero_flag));
  Multiplexer #(.select(3), .width(13), .enable("false")) multiplexer_1 (
    .in0(n1_bit_alu_1_result), .in1(n1_bit_alu_1_result), .in2(n1_bit_alu_1_result),
    .in3(n1_bit_alu_1_result), .in4(n1_bit_alu_1_result), .in6(n1_bit_alu_1_result),
    .in7(n13_bit_multiplier_1_product_s), .out(Result), .sel(ALU_Op));  // open: in5
  or or_1 (or_1_out, n1_bit_alu_1_result[0], n1_bit_alu_1_result[1], n1_bit_alu_1_result[2], n1_bit_alu_1_result[3], n1_bit_alu_1_result[4], n1_bit_alu_1_result[5], n1_bit_alu_1_result[6], n1_bit_alu_1_result[7], n1_bit_alu_1_result[8], n1_bit_alu_1_result[9], n1_bit_alu_1_result[10], n1_bit_alu_1_result[11], n1_bit_alu_1_result[12]);
  xor xor_1 (Overflow, n1_bit_alu_12_carry_out, Carry_Out);
  not not_1 (not_1_out, or_1_out);
  Multiplexer #(.select(3), .enable("false")) multiplexer_2 (
    .in0(not_1_out), .in1(not_1_out), .in2(not_1_out), .in3(not_1_out), .in4(not_1_out), .in6(not_1_out),
    .in7(n13_bit_multiplier_1_mult_zero_flag), .out(Zero_Flag), .sel(ALU_Op));  // open: in5
endmodule

module ALU_Control (
  input  B,
  input  A,
  input  F1,
  input  F0,
  output [2:0] out_5
);

  wire not_1_out, not_2_out, not_3_out, not_4_out;

  not not_1 (not_1_out, B);
  not not_2 (not_2_out, A);
  not not_3 (not_3_out, F1);
  not not_4 (not_4_out, F0);
  and and_1 (out_5[2], not_1_out, A);
  or or_1 (out_5[1], not_1_out, not_2_out);
  and and_2 (out_5[0], B, A, not_3_out, not_4_out);
endmodule

module Instruction_Control (
  input  [1:0] Opcode,
  output RegDst,
  output ALUSrc,
  output MemtoReg,
  output RegWrite,
  output MemRead,
  output MemWrite,
  output Branch,
  output ALUOp1,
  output ALUOp0
);

  wire not_1_out, not_2_out;

  not not_1 (not_1_out, Opcode[0]);
  not not_2 (not_2_out, Opcode[1]);
  and and_1 (ALUOp1, not_1_out, not_2_out);
  and and_2 (MemRead, not_2_out, Opcode[0]);
  and and_3 (MemWrite, not_1_out, Opcode[1]);
  and and_4 (ALUOp0, Opcode[0], Opcode[1]);
  or or_1 (ALUSrc, MemRead, MemWrite);
  or or_2 (RegWrite, ALUOp1, MemRead);

  assign Branch = ALUOp0;
  assign MemtoReg = MemRead;
  assign RegDst = ALUOp1;

  // Notes on the sheet:
  //   R-Format
  //   lw
  //   sw
  //   beq
endmodule

module Instruction_Fetch (
  input  [12:0] Branch_address,
  input  CLK,
  input  PCSrc,
  input  CLR,
  output [12:0] Next_instruction,
  output [12:0] Instruction
);

  wire [12:0] multiplexer_1_out, register_1_q;

  Multiplexer #(.width(13), .enable("false")) multiplexer_1 (
    .in0(Next_instruction), .in1(Branch_address), .out(multiplexer_1_out), .sel(PCSrc));
  Register_part #(.width(13)) register_1 (.D(multiplexer_1_out), .en(1'b1), .Q(register_1_q), .clk(CLK), .clr(CLR));
  ROM #(.addrWidth(13), .dataWidth(13)) rom_1 (.addr(register_1_q), .data(Instruction));  // open: sel
  Adder #(.width(13)) adder_1 (.a(13'h1), .b(register_1_q), .out(Next_instruction), .cin(1'b0));  // open: cout

  // Notes on the sheet:
  //   PC
  //   Address
  //   Instruction table
  //   1)0502- addi $0,$5,2: Stores value of 2 in register $0
  //   2)0527- addi $1,$5,7: Stores value of 7 in register $1
  //   3)0545- addi $2,$5,5: Stores value of 5 in register $2
  //   4)0568- addi $3,$5,8: Stores value of 8 in register $3
  //   5)1040-sw $2,0($0): Stores value 5 from register $2 to memory
  //   6)1160-sw $3,0($1): Stores value 8 from register $3 to memory
  //   7)09e0-lw $7,0($1): Reads value from memory and stores it into register $7
  //   8)1ca3-beq $4,$5, %L1: Checks if values of registers $4 and $5 are equal. 
  //   contents of rom_1 (hex, n*v repeats v):
  //   502 527 545 568 1040 1160 9e0 1ca3 1111
  //   If they are, it jumps to branch target address. If they aren't, it jumps to instruction right after beq.
endmodule

module Instruction_Decode (
  input  [2:0] rs,
  input  [2:0] rt,
  input  [2:0] rd,
  input  [12:0] in_4,
  input  RegDst,
  input  CLK,
  input  REGWR,
  input  [1:0] funct,
  output [12:0] out_9,
  output [12:0] out_10,
  output [12:0] offset
);

  wire [2:0] multiplexer_1_out;

  Multiplexer #(.width(3), .enable("false")) multiplexer_1 (.in0(rt), .in1(rd), .out(multiplexer_1_out), .sel(RegDst));
  assign offset = {{8{1'b0}}, {rd, funct}};  // Bit_Extender bit_extender_1
  Register register_1 (
    .Write_Register(multiplexer_1_out), .RegWrite(REGWR), .WriteData(in_4), .Read_register_1__rs(rs),
    .Read_register_2__rt(rt), .clk(CLK), .out_7(out_9), .out_8(out_10));

  // Notes on the sheet:
  //   $1
  //   0
  //   11
  //   $5
  //   $1
  //   7
  //   For instruction addi $1,$5,7: rs=101($5),rt=001($1), offset=00111(7). As op=00, RegDst=0, so rt is chosen
  //   Data from $5 and $1 are read and sent to EX stage
  //   Data from WB stage (7) is written to $1
  //   1
  //   7
  //   As op=00, RegWrite=1, and as offset=00111, it is extended to 13 bits
endmodule

module EX (
  input  [12:0] Next_address,
  input  [2:0] _010,
  input  [12:0] Read_reg_1,
  input  [12:0] Read_reg_2,
  input  [12:0] Offset,
  input  ALUSrc,
  output [12:0] Address,
  output out_8,
  output [12:0] _7,
  output out_10,
  output out_11
);

  wire [12:0] multiplexer_1_out, shifter_1_out;

  Multiplexer #(.width(13), .enable("false")) multiplexer_1 (
    .in0(Read_reg_2), .in1(Offset), .out(multiplexer_1_out), .sel(ALUSrc));
  Shifter #(.width(13)) shifter_1 (.in(Offset), .\dist (4'b0010), .out(shifter_1_out));
  _13_bit_ALU u_13_bit_alu_1 (
    .C_in(1'b0), .B_inv(1'b0), .A_inv(1'b0), .A(Read_reg_1), .B(multiplexer_1_out), .Result(_7),
    .Zero_Flag(out_8), .ALU_Op(_010), .Carry_Out(out_11), .Overflow(out_10));
  Adder #(.width(13)) adder_1 (.a(Next_address), .b(shifter_1_out), .out(Address), .cin(1'b0));  // open: cout

  // Notes on the sheet:
  //   7
  //   2
  //   0
  //   1
  //   7
  //   For addi $1,$5,7: Next address=10(2). Values from registers $5,$1, and offset are read and sent into A and B
  //   As op=00, ALUSrc=1, so offset (7) is chosen. ALU Op=010(add), so offset and $5's data are added. Result is 7
  //   Branch target address is addition of offset value shifted 2 bits left, and address of next instruction
  //   Result address is 11110(30)
  //   28
  //   30
endmodule

module MEM (
  input  [12:0] Address,
  input  [12:0] Write_Data,
  input  MemWrite,
  input  MemRead,
  input  CLK,
  output [12:0] Read_Data
);

  RAM #(.addrWidth(13), .dataWidth(13), .bus("separate")) ram_1 (
    .addr(Address), .din(Write_Data), .data(Read_Data), .str(MemWrite), .clk(CLK), .ld(MemRead));  // open: sel, clr

  // Notes on the sheet:
  //   7
  //   0
  //   For addi $1,$5,7: result of 7 is sent as address, and value of rt (7) is used as write data
  //   As op=00, MemWrite=0 and MemRead=0. So no modification is made to data memory, and no data is read from it.
  //   0
  //   X
  //   0
endmodule

module WB (
  input  [12:0] Result,
  input  [12:0] Read_Data,
  input  MemToReg,
  output [12:0] _7
);

  Multiplexer #(.width(13), .enable("false")) multiplexer_1 (.in0(Result), .in1(Read_Data), .out(_7), .sel(MemToReg));

  // Notes on the sheet:
  //   7
  //   X
  //   0
  //   For addi $1,$5,7: Data from MEM and Result from EX stages are taken as 0.
  //   As op=00, MemtoReg=0, so result of 7 is chosen to be written back to register $1.
endmodule

module Individual (
  input  [2:0] in_1,
  input  [2:0] in_2,
  input  [2:0] in_3,
  input  [2:0] in_4,
  input  in_5,
  input  [1:0] in_6,
  input  [12:0] in_7,
  input  [12:0] in_8,
  input  [12:0] in_9,
  input  in_10,
  input  in_11,
  input  in_12,
  input  [12:0] in_13,
  input  [12:0] in_14,
  input  in_15,
  input  in_16,
  input  in_17,
  input  in_18,
  input  [12:0] in_19,
  input  in_20,
  input  [12:0] in_21,
  input  in_22,
  input  in_23,
  input  in_24,
  output [12:0] out_25,
  output [12:0] out_26,
  output [12:0] out_27,
  output [12:0] out_28,
  output [12:0] out_29,
  output [12:0] out_30,
  output [12:0] out_31,
  output [12:0] out_32,
  output [12:0] out_33
);

  Instruction_Decode instruction_decode_1 (
    .rs(in_1), .rt(in_2), .rd(in_4), .in_4(in_7), .CLK(in_11), .funct(in_6), .out_9(out_25), .RegDst(in_12),
    .offset(out_28), .REGWR(in_10), .out_10(out_26));
  Instruction_Fetch instruction_fetch_1 (
    .CLR(in_23), .CLK(in_22), .Instruction(out_32), .Branch_address(out_31), .PCSrc(in_20),
    .Next_instruction(out_31));
  EX ex_1 (
    .Next_address(in_8), ._010(in_3), .Read_reg_1(in_9), .Read_reg_2(in_13), .Offset(in_14), .ALUSrc(in_15),
    .Address(out_27), ._7(out_30));  // open: out_8, out_10, out_11
  WB wb_1 (.Result(in_19), .Read_Data(in_21), .MemToReg(in_24), ._7(out_33));
  MEM mem_1 (.Address(out_27), .Write_Data(out_30), .MemWrite(in_17), .CLK(in_16), .Read_Data(out_29), .MemRead(in_18));
endmodule

module Register (
  input  clk,
  input  [2:0] Read_register_1__rs,
  input  [2:0] Write_Register,
  input  [2:0] Read_register_2__rt,
  input  RegWrite,
  input  [12:0] WriteData,
  output [12:0] out_7,
  output [12:0] out_8
);

  wire and_1_out, and_2_out, and_3_out, and_4_out, and_5_out, and_6_out, and_7_out, and_8_out,
       decoder_1_out0, decoder_1_out1, decoder_1_out2, decoder_1_out3, decoder_1_out4, decoder_1_out5,
       decoder_1_out6, decoder_1_out7;
  wire [12:0] _0_q, _1_q, _2_q, _3_q, _4_q, _5_q, _6_q, _7_q;

  Decoder #(.select(3)) decoder_1 (
    .out0(decoder_1_out0), .out1(decoder_1_out1), .out2(decoder_1_out2), .out3(decoder_1_out3),
    .out4(decoder_1_out4), .out5(decoder_1_out5), .out6(decoder_1_out6), .out7(decoder_1_out7),
    .sel(Write_Register));  // open: en
  and and_1 (and_1_out, decoder_1_out0, RegWrite);
  and and_2 (and_2_out, decoder_1_out1, RegWrite);
  and and_3 (and_3_out, decoder_1_out2, RegWrite);
  and and_4 (and_4_out, decoder_1_out3, RegWrite);
  and and_5 (and_5_out, decoder_1_out4, RegWrite);
  and and_6 (and_6_out, decoder_1_out5, RegWrite);
  and and_7 (and_7_out, decoder_1_out6, RegWrite);
  and and_8 (and_8_out, decoder_1_out7, RegWrite);
  Register_part #(.width(13)) _0 (.D(WriteData), .en(and_1_out), .Q(_0_q), .clk(clk));  // open: clr
  Register_part #(.width(13)) _1 (.D(WriteData), .en(and_2_out), .Q(_1_q), .clk(clk));  // open: clr
  Register_part #(.width(13)) _2 (.D(WriteData), .en(and_3_out), .Q(_2_q), .clk(clk));  // open: clr
  Register_part #(.width(13)) _3 (.D(WriteData), .en(and_4_out), .Q(_3_q), .clk(clk));  // open: clr
  Register_part #(.width(13)) _4 (.D(WriteData), .en(and_5_out), .Q(_4_q), .clk(clk));  // open: clr
  Register_part #(.width(13)) _5 (.D(WriteData), .en(and_6_out), .Q(_5_q), .clk(clk));  // open: clr
  Register_part #(.width(13)) _6 (.D(WriteData), .en(and_7_out), .Q(_6_q), .clk(clk));  // open: clr
  Register_part #(.width(13)) _7 (.D(WriteData), .en(and_8_out), .Q(_7_q), .clk(clk));  // open: clr
  Multiplexer #(.select(3), .width(13)) multiplexer_1 (
    .in0(_0_q), .in1(_1_q), .in2(_2_q), .in3(_3_q), .in4(_4_q), .in5(_5_q), .in6(_6_q), .in7(_7_q),
    .out(out_7), .sel(Read_register_1__rs));  // open: en
  Multiplexer #(.select(3), .width(13)) multiplexer_2 (
    .in0(_0_q), .in1(_1_q), .in2(_2_q), .in3(_3_q), .in4(_4_q), .in5(_5_q), .in6(_6_q), .in7(_7_q),
    .out(out_8), .sel(Read_register_2__rt));  // open: en
endmodule

module Instruction_Control_new (
  input  [2:0] Opcode,
  output RegDst,
  output RegWrite,
  output ALUSrc,
  output MemRead,
  output MemWrite,
  output MemtoReg,
  output Branch,
  output [1:0] ALUOp
);

  wire addi_out, not_1_out, not_2_out, not_3_out;

  not not_1 (not_1_out, Opcode[2]);
  not not_2 (not_2_out, Opcode[1]);
  not not_3 (not_3_out, Opcode[0]);
  and R_type (RegDst, not_1_out, not_2_out, not_3_out);
  and lw (MemRead, not_1_out, not_2_out, Opcode[0]);
  and sw (MemWrite, not_1_out, Opcode[1], not_3_out);
  and beq (ALUOp[0], not_1_out, Opcode[1], Opcode[0]);
  and addi (addi_out, Opcode[2], not_2_out, not_3_out);
  or or_1 (ALUOp[1], RegDst, addi_out);
  or or_2 (RegWrite, RegDst, MemRead, addi_out);
  or or_3 (ALUSrc, MemRead, MemWrite, addi_out);

  assign Branch = ALUOp[0];
  assign MemtoReg = MemRead;
endmodule
